// Digital circuit PDP8-X.dig as structural Verilog
module PDP8_X (
  input  clk
);

  wire AC2RAMD, AC_CK, add_1_c_o, add_2_c_o, AND, and_1_out, and_20_out, and_21_out, and_23_out, and_25_out,
       and_27_out, and_28_out, and_29_out, and_31_out, and_33_out, and_34_out, and_35_out, and_36_out,
       and_37_out, and_38_out, and_40_out, and_42_out, and_45_out, and_46_out, and_47_out, and_49_out,
       and_50_out, and_51_out, and_52_out, and_53_out, and_54_out, and_55_out, and_56_out, and_57_out,
       and_59_out, and_60_out, and_61_out, and_62_out, and_64_out, and_65_out, and_66_out, and_67_out,
       and_68_out, and_69_out, and_71_out, and_72_out, and_73_out, and_74_out, and_75_out, and_76_out,
       and_77_out, and_78_out, and_79_out, and_81_out, and_82_out, and_84_out, and_85_out, and_86_out,
       and_87_out, and_89_out, and_90_out, and_91_out, and_92_out, and_94_out, and_95_out, and_96_out,
       and_97_out, and_99_out, and_100_out, and_101_out, and_102_out, and_103_out, and_104_out, and_106_out,
       and_107_out, and_108_out, and_109_out, and_110_out, and_111_out, and_112_out, and_113_out,
       and_114_out, and_116_out, and_118_out, and_120_out, and_121_out, and_122_out, and_123_out,
       and_125_out, and_127_out, and_128_out, AUTOIND, BP_ENABLED_b, CLA, CLAx, CNT_AND, CNT_AND_I,
       CNT_AND_IA, CNT_DCA, CNT_DCA_I, CNT_DCA_IA, CNT_ISZ, CNT_ISZ_I, CNT_ISZ_IA, CNT_JMP, CNT_JMP_I,
       CNT_JMP_IA, CNT_JMS, CNT_JMS_I, CNT_JMS_IA, CNT_OPR1, CNT_OPR2, CNT_TAD, CNT_TAD_I, CNT_TAD_IA,
       comparator_1_eq, comparator_2_eq, counter_1_o1, counter_1_o2, counter_1_o3, counter_1_o4,
       counter_1_o5, counter_1_o6, counter_1_o7, counter_1_o8, counter_1_o9, counter_1_o10, counter_1_o11,
       counter_1_o12, counter_1_o13, counter_1_o14, counter_1_o15, counter_1_o16, counter_1_o17,
       counter_1_o18, counter_1_o19, counter_1_o20, counter_1_o21, counter_1_o22, counter_1_o23,
       counter_1_o24, counter_1_o25, counter_1_o26, counter_1_o27, counter_1_o28, counter_1_o29,
       counter_1_o30, counter_1_o31, counter_1_o32, d_ff_1_q, DATA_CK, DCA, demultiplexer_1_out_0,
       demultiplexer_1_out_1, demultiplexer_1_out_2, demultiplexer_1_out_3, demultiplexer_1_out_4,
       demultiplexer_1_out_5, demultiplexer_1_out_6, demultiplexer_1_out_7, demultiplexer_2_out_3,
       demultiplexer_2_out_7, demultiplexer_3_out_3, demultiplexer_3_out_7, demultiplexer_4_out_10,
       demultiplexer_4_out_11, demultiplexer_4_out_12, demultiplexer_4_out_13, demultiplexer_4_out_14,
       demultiplexer_4_out_15, demultiplexer_4_out_16, demultiplexer_4_out_17, demultiplexer_4_out_18,
       demultiplexer_4_out_19, demultiplexer_4_out_20, demultiplexer_4_out_21, demultiplexer_4_out_22,
       demultiplexer_4_out_23, demultiplexer_4_out_24, demultiplexer_4_out_25, demultiplexer_4_out_26,
       demultiplexer_4_out_27, demultiplexer_4_out_28, demultiplexer_4_out_29, demultiplexer_4_out_30,
       demultiplexer_4_out_31, demultiplexer_4_out_32, demultiplexer_4_out_33, demultiplexer_4_out_34,
       demultiplexer_4_out_35, demultiplexer_4_out_36, demultiplexer_4_out_37, demultiplexer_4_out_38,
       demultiplexer_4_out_39, demultiplexer_4_out_40, demultiplexer_4_out_41, demultiplexer_4_out_42,
       demultiplexer_4_out_43, demultiplexer_4_out_44, demultiplexer_4_out_45, demultiplexer_4_out_46,
       demultiplexer_4_out_47, demultiplexer_4_out_48, demultiplexer_4_out_49, demultiplexer_4_out_50,
       demultiplexer_4_out_51, demultiplexer_4_out_52, demultiplexer_4_out_53, demultiplexer_4_out_54,
       demultiplexer_4_out_55, demultiplexer_4_out_56, demultiplexer_4_out_57, demultiplexer_4_out_58,
       demultiplexer_4_out_59, demultiplexer_4_out_60, demultiplexer_4_out_61, demultiplexer_4_out_62,
       demultiplexer_4_out_63, driver_29_out, driver_30_out, driver_61_out, driver_62_out, driver_63_out,
       driver_67_out, driver_68_out, driver_72_out, driver_73_out, driver_97_out, driver_98_out,
       driver_287_out, driver_288_out, driver_293_out, driver_311_out, driver_312_out, driver_313_out,
       driver_317_out, driver_318_out, driver_322_out, driver_323_out, driver_327_out, driver_328_out,
       driver_333_out, driver_338_out, driver_341_out, driver_342_out, driver_343_out, driver_347_out,
       driver_348_out, driver_349_out, driver_350_out, driver_351_out, driver_352_out, driver_353_out,
       driver_355_out, driver_356_out, driver_357_out, driver_362_out, driver_363_out, driver_368_out,
       driver_372_out, driver_373_out, driver_383_out, driver_386_out, driver_387_out, driver_388_out,
       driver_390_out, driver_391_out, driver_392_out, driver_396_out, driver_397_out, driver_398_out,
       driver_402_out, driver_403_out, driver_408_out, driver_412_out, driver_413_out, driver_418_out,
       driver_422_out, driver_423_out, driver_433_out, driver_436_out, driver_437_out, driver_438_out,
       driver_440_out, driver_441_out, driver_442_out, driver_445_out, driver_446_out, driver_447_out,
       driver_448_out, driver_452_out, driver_453_out, driver_457_out, driver_458_out, driver_466_out,
       driver_467_out, driver_468_out, driver_472_out, driver_473_out, driver_477_out, driver_478_out,
       driver_482_out, driver_483_out, FLAG_PRNRDY, H_out, HALT, HLT_ENABLED_b, I_out, INC2RAMD, INCZERO,
       IND, IND2INC, IND2PC, IND2RAMA, IND_CK, INST_KCC, INST_KCF, INST_KIE, INST_KRB, INST_KRS, INST_KSF,
       INST_TCF, INST_TFL, INST_TLS, INST_TPC, INST_TSF, INST_TSK, IOT, IOT_1x, IOT_2x, IOT_3x, IOT_4x,
       IOT_5, IOT_5x, IOT_6, IOT_6x, IOT_7, IOT_8, IOT_9, IOT_DEVCPU, IOT_DEVHSP, IOT_DEVHSR, IOT_DEVKBD,
       IOT_DEVPRI, IR2PC, IR2RAMA, IR_CK, ISZ, JMP, JMS, LD2INC, LINK, LINK_CK, monoflop_1_nq, monoflop_1_q,
       monoflop_2_q, monoflop_3_q, monoflop_4_q, monoflop_5_q, NOIND, nor_2_out, NOTNOP, OPR, OPR1, OPR2,
       OPR_CLA1, OPR_CLA2, OPR_CLL, OPR_CMA, OPR_CML, OPR_HLT, OPR_IAC, OPR_LEFT, OPR_NA1, OPR_NOP, OPR_OSR,
       OPR_RIGHT, OPR_SMA, OPR_SNL, OPR_SZA, OPR_TSTINV, OPR_X2, or_1_out, or_9_out, or_10_out, or_11_out,
       or_12_out, or_13_out, or_14_out, or_15_out, or_17_out, or_18_out, PC2RAMA, PC2RAMD, PC_CK, PC_eq_200,
       PC_LD, PH00, PH01, PH02, PH03, PH04, PH05, PH06, PH07, PH08, PH09, PH10, PH11, PH12, PH13, PH14, PH15,
       R_out, RAM_OE, RAM_WE, RAMA_HOLD, RAMD2AC_ADD, RAMD2AC_AND, RAMD2IND, RAMD2PC, reset_1_out, ROT2AC,
       rotater_1_p3, rotater_1_p5, rs_ff_as_2_q, rs_ff_as_3_q, S_out, SKIP, TAD, xor_1_out, xor_2_out;
  wire [2:0] DA0, DA1, DA2, DA3, IND0, IND1, IND2, IND3, RA0, RA1, RA2, RA3;
  wire [3:0] counter_2_out;
  wire [11:0] AC, add_1_s, add_2_s, and_30_out, and_39_out, and_43_out, autocapture_1__10, autocapture_1__11,
       autocapture_1__12, autocapture_1__13, autocapture_1__14, autocapture_1__15, autocapture_1__16,
       autocapture_1__17, bitextender_1_out, bitextender_2_out, bitextender_3_out, BUS_IR, BUS_PC,
       dipswitch_1_out, driver_24_out, driver_56_out, INC_s, LATCHEDDATA, not_2_out, or_16_out, PCIN,
       RAMDATA, register_1_q, rotater_1_p4, xor_3_out;
  wire [31:0] COUNT_out, INSTRUCTION_COUNT_out;

  Demultiplexer #(.Selector_Bits(3)) demultiplexer_1 (
    .sel(BUS_IR[2:0]), .in(IOT_DEVHSR), .out_0(demultiplexer_1_out_0), .out_1(demultiplexer_1_out_1),
    .out_2(demultiplexer_1_out_2), .out_3(demultiplexer_1_out_3), .out_4(demultiplexer_1_out_4),
    .out_5(demultiplexer_1_out_5), .out_6(demultiplexer_1_out_6), .out_7(demultiplexer_1_out_7));
  LED led_1 (.in(IOT_DEVHSR));
  or or_1 (or_1_out, PH02, PH03, PH04, PH05, PH06, PH07, PH08, PH09, PH10, PH11);
  LED led_2 (.in(IOT));
  // Probe on BUS_IR[2:0]
  // Probe on BUS_IR[8:3]
  and and_1 (and_1_out, or_1_out, IOT);
  Demultiplexer #(.Selector_Bits(3)) demultiplexer_2 (
    .sel(BUS_IR[2:0]), .in(IOT_DEVKBD), .out_0(INST_KCF), .out_1(INST_KSF), .out_2(INST_KCC),
    .out_3(demultiplexer_2_out_3), .out_4(INST_KRS), .out_5(INST_KIE), .out_6(INST_KRB),
    .out_7(demultiplexer_2_out_7));
  LED led_3 (.in(IOT_DEVKBD));
  Demultiplexer #(.Selector_Bits(3)) demultiplexer_3 (
    .sel(BUS_IR[2:0]), .in(IOT_DEVPRI), .out_0(INST_TFL), .out_1(INST_TSF), .out_2(INST_TCF),
    .out_3(demultiplexer_3_out_3), .out_4(INST_TPC), .out_5(INST_TSK), .out_6(INST_TLS),
    .out_7(demultiplexer_3_out_7));
  LED led_4 (.in(IOT_DEVPRI));
  Demultiplexer #(.Selector_Bits(6)) demultiplexer_4 (
    .sel(BUS_IR[8:3]), .in(and_1_out), .out_0(IOT_DEVCPU), .out_1(IOT_DEVHSR), .out_2(IOT_DEVHSP),
    .out_3(IOT_DEVKBD), .out_4(IOT_DEVPRI), .out_5(IOT_5), .out_6(IOT_6), .out_7(IOT_7), .out_8(IOT_8),
    .out_9(IOT_9), .out_10(demultiplexer_4_out_10), .out_11(demultiplexer_4_out_11),
    .out_12(demultiplexer_4_out_12), .out_13(demultiplexer_4_out_13), .out_14(demultiplexer_4_out_14),
    .out_15(demultiplexer_4_out_15), .out_16(demultiplexer_4_out_16), .out_17(demultiplexer_4_out_17),
    .out_18(demultiplexer_4_out_18), .out_19(demultiplexer_4_out_19), .out_20(demultiplexer_4_out_20),
    .out_21(demultiplexer_4_out_21), .out_22(demultiplexer_4_out_22), .out_23(demultiplexer_4_out_23),
    .out_24(demultiplexer_4_out_24), .out_25(demultiplexer_4_out_25), .out_26(demultiplexer_4_out_26),
    .out_27(demultiplexer_4_out_27), .out_28(demultiplexer_4_out_28), .out_29(demultiplexer_4_out_29),
    .out_30(demultiplexer_4_out_30), .out_31(demultiplexer_4_out_31), .out_32(demultiplexer_4_out_32),
    .out_33(demultiplexer_4_out_33), .out_34(demultiplexer_4_out_34), .out_35(demultiplexer_4_out_35),
    .out_36(demultiplexer_4_out_36), .out_37(demultiplexer_4_out_37), .out_38(demultiplexer_4_out_38),
    .out_39(demultiplexer_4_out_39), .out_40(demultiplexer_4_out_40), .out_41(demultiplexer_4_out_41),
    .out_42(demultiplexer_4_out_42), .out_43(demultiplexer_4_out_43), .out_44(demultiplexer_4_out_44),
    .out_45(demultiplexer_4_out_45), .out_46(demultiplexer_4_out_46), .out_47(demultiplexer_4_out_47),
    .out_48(demultiplexer_4_out_48), .out_49(demultiplexer_4_out_49), .out_50(demultiplexer_4_out_50),
    .out_51(demultiplexer_4_out_51), .out_52(demultiplexer_4_out_52), .out_53(demultiplexer_4_out_53),
    .out_54(demultiplexer_4_out_54), .out_55(demultiplexer_4_out_55), .out_56(demultiplexer_4_out_56),
    .out_57(demultiplexer_4_out_57), .out_58(demultiplexer_4_out_58), .out_59(demultiplexer_4_out_59),
    .out_60(demultiplexer_4_out_60), .out_61(demultiplexer_4_out_61), .out_62(demultiplexer_4_out_62),
    .out_63(demultiplexer_4_out_63));
  or or_2 (IOT_5x, demultiplexer_4_out_50, demultiplexer_4_out_51, demultiplexer_4_out_52, demultiplexer_4_out_53, demultiplexer_4_out_54, demultiplexer_4_out_56, demultiplexer_4_out_57, demultiplexer_4_out_58, demultiplexer_4_out_59, demultiplexer_4_out_55);
  or or_3 (IOT_6x, demultiplexer_4_out_60, demultiplexer_4_out_61, demultiplexer_4_out_63, demultiplexer_4_out_62);
  assign PC2RAMA = PH00 ? PH00 : 1'bz;  // Driver driver_1
  assign RAM_OE = PH00 ? PH00 : 1'bz;  // Driver driver_2
  assign PC2RAMA = PH01 ? PH01 : 1'bz;  // Driver driver_3
  assign RAM_OE = PH01 ? PH01 : 1'bz;  // Driver driver_4
  assign IR_CK = PH01 ? PH01 : 1'bz;  // Driver driver_5
  assign PC_CK = PH01 ? PH01 : 1'bz;  // Driver driver_6
  or or_4 (IOT_3x, demultiplexer_4_out_30, demultiplexer_4_out_31, demultiplexer_4_out_32, demultiplexer_4_out_33, demultiplexer_4_out_34, demultiplexer_4_out_36, demultiplexer_4_out_37, demultiplexer_4_out_38, demultiplexer_4_out_39, demultiplexer_4_out_35);
  or or_5 (IOT_4x, demultiplexer_4_out_40, demultiplexer_4_out_41, demultiplexer_4_out_42, demultiplexer_4_out_43, demultiplexer_4_out_44, demultiplexer_4_out_46, demultiplexer_4_out_47, demultiplexer_4_out_48, demultiplexer_4_out_49, demultiplexer_4_out_45);
  or or_6 (IOT_1x, demultiplexer_4_out_10, demultiplexer_4_out_11, demultiplexer_4_out_12, demultiplexer_4_out_13, demultiplexer_4_out_14, demultiplexer_4_out_16, demultiplexer_4_out_17, demultiplexer_4_out_18, demultiplexer_4_out_19, demultiplexer_4_out_15);
  or or_7 (IOT_2x, demultiplexer_4_out_20, demultiplexer_4_out_21, demultiplexer_4_out_22, demultiplexer_4_out_23, demultiplexer_4_out_24, demultiplexer_4_out_26, demultiplexer_4_out_27, demultiplexer_4_out_28, demultiplexer_4_out_29, demultiplexer_4_out_25);
  // Probe on BUS_IR
  LED led_5 (.in(OPR));
  LED led_6 (.in(OPR1));
  LED led_7 (.in(OPR2));
  Demultiplexer #(.Selector_Bits(3)) demultiplexer_5 (
    .sel(BUS_IR[11:9]), .in(1'b1), .out_0(AND), .out_1(TAD), .out_2(ISZ), .out_3(DCA), .out_4(JMS),
    .out_5(JMP), .out_6(IOT), .out_7(OPR));
  Demultiplexer demultiplexer_6 (.sel(BUS_IR[8]), .in(OPR), .out_0(OPR1), .out_1(OPR2));
  and and_2 (AUTOIND, BUS_IR[3], ~BUS_IR[4], ~BUS_IR[5], ~BUS_IR[6], ~BUS_IR[7], BUS_IR[8]);  // And
  not not_1 (NOIND, BUS_IR[8]);
  LED led_8 (.in(AUTOIND));
  nor nor_1 (IND, AUTOIND, NOIND);
  and and_3 (OPR_IAC, BUS_IR[0], OPR1);
  and and_4 (OPR_X2, BUS_IR[1], OPR1);
  and and_5 (OPR_LEFT, BUS_IR[2], OPR1);
  and and_6 (OPR_RIGHT, BUS_IR[3], OPR1);
  and and_7 (OPR_CML, BUS_IR[4], OPR1);
  and and_8 (OPR_CMA, BUS_IR[5], OPR1);
  and and_9 (OPR_CLL, BUS_IR[6], OPR1);
  and and_10 (OPR_CLA1, BUS_IR[7], OPR1);
  and and_11 (OPR_NA1, BUS_IR[0], OPR2);
  and and_12 (OPR_HLT, BUS_IR[1], OPR2);
  and and_13 (OPR_OSR, BUS_IR[2], OPR2);
  and and_14 (OPR_TSTINV, BUS_IR[3], OPR2);
  and and_15 (OPR_SNL, BUS_IR[4], OPR2);
  and and_16 (OPR_SZA, BUS_IR[5], OPR2);
  and and_17 (OPR_SMA, BUS_IR[6], OPR2);
  and and_18 (OPR_CLA2, BUS_IR[7], OPR2);
  or or_8 (NOTNOP, BUS_IR[0], BUS_IR[1], BUS_IR[2], BUS_IR[3], BUS_IR[4], BUS_IR[5], BUS_IR[6], BUS_IR[7]);
  and and_19 (OPR_NOP, NOTNOP, OPR);
  LED led_9 (.in(IND));
  LED led_10 (.in(OPR_IAC));
  LED led_11 (.in(OPR_X2));
  LED led_12 (.in(OPR_LEFT));
  LED led_13 (.in(OPR_RIGHT));
  LED led_14 (.in(OPR_CML));
  LED led_15 (.in(OPR_CMA));
  LED led_16 (.in(OPR_CLL));
  LED led_17 (.in(OPR_CLA1));
  LED led_18 (.in(OPR_NA1));
  LED led_19 (.in(OPR_HLT));
  LED led_20 (.in(OPR_OSR));
  LED led_21 (.in(OPR_TSTINV));
  LED led_22 (.in(OPR_SNL));
  LED led_23 (.in(OPR_SZA));
  LED led_24 (.in(OPR_SMA));
  LED led_25 (.in(OPR_CLA2));
  LED led_26 (.in(OPR_NOP));
  PullDown pulldown_1 (.out(PC_LD));
  PullDown pulldown_2 (.out(IR2PC));
  PullDown pulldown_3 (.out(IR2PC));
  PullDown pulldown_4 (.out(IND_CK));
  PullDown pulldown_5 (.out(IND2PC));
  PullDown pulldown_6 (.out(IR2RAMA));
  PullDown pulldown_7 (.out(IR2RAMA));
  PullDown pulldown_8 (.out(AC_CK));
  PullDown pulldown_9 (.out(LINK_CK));
  PullDown pulldown_10 (.out(RAMD2PC));
  PullDown pulldown_11 (.out(IND2RAMA));
  PullDown pulldown_12 (.out(INC2RAMD));
  PullDown pulldown_13 (.out(IR_CK));
  PullDown pulldown_14 (.out(RAM_WE));
  PullDown pulldown_15 (.out(PC_CK));
  PullDown pulldown_16 (.out(PC2RAMD));
  PullDown pulldown_17 (.out(ROT2AC));
  PullDown pulldown_18 (.out(RAMD2AC_ADD));
  PullDown pulldown_19 (.out(RAM_OE));
  PullDown pulldown_20 (.out(RAMA_HOLD));
  PullDown pulldown_21 (.out(IND2INC));
  PullDown pulldown_22 (.out(LD2INC));
  PullDown pulldown_23 (.out(DATA_CK));
  Comparator #(.Bits(12)) comparator_1 (.a({RA3, RA2, RA1, RA0}), .b(12'h5e), .eq(comparator_1_eq));  // open: gt, lt
  and and_20 (and_20_out, comparator_1_eq, RAM_WE);
  COUNTER counter_1 (
    .i1(CNT_AND), .i2(CNT_AND_I), .i3(CNT_AND_IA), .i4(CNT_TAD), .i5(CNT_TAD_I), .i6(CNT_TAD_IA),
    .i7(CNT_ISZ), .i8(CNT_ISZ_I), .i9(CNT_ISZ_IA), .i10(CNT_DCA), .i11(CNT_DCA_I), .i12(CNT_DCA_IA),
    .i13(CNT_JMS), .i14(CNT_JMS_I), .i15(CNT_JMS_IA), .i16(CNT_JMP), .i17(CNT_JMP_I), .i18(CNT_JMP_IA),
    .i19(CNT_OPR1), .i20(CNT_OPR2), .i21(IOT_DEVCPU), .i22(IOT_DEVHSR), .i23(IOT_DEVHSP), .i24(IOT_DEVKBD),
    .i25(IOT_DEVPRI), .i26(IOT_5), .i27(IOT_6), .i28(IOT_7), .i29(IOT_8), .i30(IOT_9), .i31(IOT_1x),
    .i32(IOT_2x), .C(1'b0), .E(PH02), .o1(counter_1_o1), .o2(counter_1_o2), .o3(counter_1_o3),
    .o4(counter_1_o4), .o5(counter_1_o5), .o6(counter_1_o6), .o7(counter_1_o7), .o8(counter_1_o8),
    .o9(counter_1_o9), .o10(counter_1_o10), .o11(counter_1_o11), .o12(counter_1_o12), .o13(counter_1_o13),
    .o14(counter_1_o14), .o15(counter_1_o15), .o16(counter_1_o16), .o17(counter_1_o17), .o18(counter_1_o18),
    .o19(counter_1_o19), .o20(counter_1_o20), .o21(counter_1_o21), .o22(counter_1_o22), .o23(counter_1_o23),
    .o24(counter_1_o24), .o25(counter_1_o25), .o26(counter_1_o26), .o27(counter_1_o27), .o28(counter_1_o28),
    .o29(counter_1_o29), .o30(counter_1_o30), .o31(counter_1_o31), .o32(counter_1_o32));
  AUTOCAPTURE autocapture_1 (
    .D(RAMDATA), .A({RA3, RA2, RA1, RA0}), .WR(RAM_WE), ._10(autocapture_1__10), ._11(autocapture_1__11),
    ._12(autocapture_1__12), ._13(autocapture_1__13), ._14(autocapture_1__14), ._15(autocapture_1__15),
    ._16(autocapture_1__16), ._17(autocapture_1__17));
  Counter #(.Bits(32)) INSTRUCTION_COUNT (.en(1'b1), .C(PH01), .clr(1'b0), .out(INSTRUCTION_COUNT_out));  // open: ovf
  Register #(.Bits(12)) register_1 (.D(RAMDATA), .C(and_20_out), .en(1'b1), .Q(register_1_q));
  // Probe on counter_1_o1
  // Probe on counter_1_o2
  // Probe on counter_1_o3
  // Probe on counter_1_o4
  // Probe on counter_1_o5
  // Probe on counter_1_o6
  // Probe on counter_1_o7
  // Probe on counter_1_o8
  // Probe on counter_1_o9
  // Probe on counter_1_o10
  // Probe on counter_1_o11
  // Probe on counter_1_o12
  // Probe on counter_1_o13
  // Probe on counter_1_o14
  // Probe on counter_1_o15
  // Probe on counter_1_o16
  // Probe on counter_1_o17
  // Probe on counter_1_o18
  // Probe on counter_1_o19
  // Probe on counter_1_o20
  // Probe on counter_1_o21
  // Probe on counter_1_o22
  // Probe on counter_1_o23
  // Probe on counter_1_o24
  // Probe on counter_1_o25
  // Probe on counter_1_o26
  // Probe on counter_1_o27
  // Probe on counter_1_o28
  // Probe on counter_1_o29
  // Probe on counter_1_o30
  // Probe on counter_1_o31
  // Probe on counter_1_o32
  // Probe on autocapture_1__10
  // Probe on autocapture_1__11
  // Probe on autocapture_1__12
  // Probe on autocapture_1__13
  // Probe on autocapture_1__14
  // Probe on autocapture_1__15
  // Probe on autocapture_1__16
  // Probe on autocapture_1__17
  // Probe on INSTRUCTION_COUNT_out
  // Probe on register_1_q
  Seven_Seg_Hex seven_seg_hex_1 (.d({1'b0, BUS_PC[11:9]}), .dp(1'b0));
  Seven_Seg_Hex seven_seg_hex_2 (.d({1'b0, BUS_IR[11:9]}), .dp(1'b0));
  Seven_Seg_Hex seven_seg_hex_3 (.d({1'b0, AC[11:9]}), .dp(1'b0));
  Seven_Seg_Hex seven_seg_hex_4 (.d({1'b0, IND3}), .dp(1'b0));
  Seven_Seg_Hex seven_seg_hex_5 (.d({1'b0, RA3}), .dp(1'b0));
  Seven_Seg_Hex seven_seg_hex_6 (.d({1'b0, RAMDATA[11:9]}), .dp(1'b0));
  Seven_Seg_Hex seven_seg_hex_7 (.d({1'b0, PCIN[11:9]}), .dp(1'b0));
  Seven_Seg_Hex seven_seg_hex_8 (.d({1'b0, DA3}), .dp(1'b0));
  or or_9 (or_9_out, INST_TPC, INST_TLS);
  Seven_Seg_Hex seven_seg_hex_9 (.d({1'b0, BUS_PC[8:6]}), .dp(1'b0));
  Seven_Seg_Hex seven_seg_hex_10 (.d({1'b0, BUS_IR[8:6]}), .dp(1'b0));
  Seven_Seg_Hex seven_seg_hex_11 (.d({1'b0, AC[8:6]}), .dp(1'b0));
  Seven_Seg_Hex seven_seg_hex_12 (.d({1'b0, IND2}), .dp(1'b0));
  Seven_Seg_Hex seven_seg_hex_13 (.d({1'b0, RA2}), .dp(1'b0));
  Seven_Seg_Hex seven_seg_hex_14 (.d({1'b0, RAMDATA[8:6]}), .dp(1'b0));
  Seven_Seg_Hex seven_seg_hex_15 (.d({1'b0, PCIN[8:6]}), .dp(1'b0));
  Seven_Seg_Hex seven_seg_hex_16 (.d({1'b0, DA2}), .dp(1'b0));
  Seven_Seg_Hex seven_seg_hex_17 (.d({1'b0, BUS_PC[5:3]}), .dp(1'b0));
  Seven_Seg_Hex seven_seg_hex_18 (.d({1'b0, BUS_IR[5:3]}), .dp(1'b0));
  Seven_Seg_Hex seven_seg_hex_19 (.d({1'b0, AC[5:3]}), .dp(1'b0));
  Seven_Seg_Hex seven_seg_hex_20 (.d({1'b0, IND1}), .dp(1'b0));
  Seven_Seg_Hex seven_seg_hex_21 (.d({1'b0, RA1}), .dp(1'b0));
  Seven_Seg_Hex seven_seg_hex_22 (.d({1'b0, RAMDATA[5:3]}), .dp(1'b0));
  Seven_Seg_Hex seven_seg_hex_23 (.d({1'b0, PCIN[5:3]}), .dp(1'b0));
  Seven_Seg_Hex seven_seg_hex_24 (.d({1'b0, DA1}), .dp(1'b0));
  Monoflop #(.timerDelay(300)) monoflop_1 (.C(or_9_out), .R(1'b0), .Q(monoflop_1_q), .nQ(monoflop_1_nq));
  Seven_Seg_Hex seven_seg_hex_25 (.d({1'b0, BUS_PC[2:0]}), .dp(1'b0));
  Seven_Seg_Hex seven_seg_hex_26 (.d({1'b0, BUS_IR[2:0]}), .dp(1'b0));
  Seven_Seg_Hex seven_seg_hex_27 (.d({1'b0, AC[2:0]}), .dp(1'b0));
  Seven_Seg_Hex seven_seg_hex_28 (.d({1'b0, IND0}), .dp(1'b0));
  Seven_Seg_Hex seven_seg_hex_29 (.d({1'b0, RA0}), .dp(1'b0));
  Seven_Seg_Hex seven_seg_hex_30 (.d({1'b0, RAMDATA[2:0]}), .dp(1'b0));
  Seven_Seg_Hex seven_seg_hex_31 (.d({1'b0, PCIN[2:0]}), .dp(1'b0));
  Seven_Seg_Hex seven_seg_hex_32 (.d({1'b0, DA0}), .dp(1'b0));
  Counter #(.Bits(32)) COUNT (.en(1'b1), .C(or_9_out), .clr(1'b0), .out(COUNT_out));  // open: ovf
  Terminal #(.termWidth(20), .termHeight(10)) PRN (.D(AC[7:0]), .C(or_9_out), .en(1'b1));
  LED led_27 (.in(LINK));
  // Probe on COUNT_out
  LED led_28 (.in(INST_KCF));
  LED led_29 (.in(OPR_CLA1));
  LED led_30 (.in(AND));
  Monoflop monoflop_2 (.C(monoflop_1_q), .R(1'b0), .Q(monoflop_2_q));  // open: nQ
  Monoflop monoflop_3 (.C(monoflop_1_nq), .R(1'b0), .Q(monoflop_3_q));  // open: nQ
  assign PC_CK = PC_eq_200 ? PC_eq_200 : 1'bz;  // Driver driver_7
  assign PC_LD = PC_eq_200 ? PC_eq_200 : 1'bz;  // Driver driver_8
  LED led_31 (.in(INST_KSF));
  LED led_32 (.in(OPR_CLL));
  LED led_33 (.in(TAD));
  or or_10 (or_10_out, INST_TFL, monoflop_2_q);
  or or_11 (or_11_out, monoflop_3_q, INST_TCF);
  LED led_34 (.in(IR2PC));
  assign PCIN = PC_eq_200 ? 12'h80 : 12'bz;  // Driver driver_9
  LED led_35 (.in(INST_KCC));
  LED led_36 (.in(INST_KRS));
  LED led_37 (.in(OPR_CMA));
  LED led_38 (.in(OPR_CML));
  LED led_39 (.in(ISZ));
  LED led_40 (.in(DCA));
  RS_FF_AS rs_ff_as_1 (.S(or_10_out), .R(or_11_out), .nQ(FLAG_PRNRDY));  // open: Q
  // OC12 oc12_1: pin names not known; wires that end beside it: BUS_IR[6:0], BUS_PC[11:7], BUS_IR[7], IR2PC, PCIN[6:0], PCIN[11:7], PCIN
  LED led_41 (.in(INST_KIE));
  LED led_42 (.in(OPR_IAC));
  LED led_43 (.in(JMS));
  LED led_44 (.in(INST_KRB));
  LED led_45 (.in(OPR_RIGHT));
  LED led_46 (.in(JMP));
  Button S (.out(S_out));
  Button I (.out(I_out));
  Button R (.out(R_out));
  Button H (.out(H_out));
  Button button_1 (.out(PC_eq_200));
  // Probe on PCIN
  LED led_47 (.in(PC_CK));
  LED led_48 (.in(PC_LD));
  LED led_49 (.in(RAMD2PC));
  assign PCIN = RAMD2PC ? {DA3, DA2, DA1, DA0} : 12'bz;  // Driver driver_10
  LED led_50 (.in(IND2PC));
  assign PCIN = IND2PC ? {IND3, IND2, IND1, IND0} : 12'bz;  // Driver driver_11
  LED led_51 (.in(INST_TFL));
  LED led_52 (.in(OPR_LEFT));
  LED led_53 (.in(OPR_X2));
  LED led_54 (.in(IOT));
  LED led_55 (.in(OPR));
  Monoflop #(.timerDelay(2)) monoflop_4 (.C(I_out), .R(1'b0), .Q(monoflop_4_q));  // open: nQ
  Monoflop monoflop_5 (.C(R_out), .R(1'b0), .Q(monoflop_5_q));  // open: nQ
  Comparator #(.Bits(12)) comparator_2 (.a(BUS_PC), .b(12'h698), .eq(comparator_2_eq));  // open: gt, lt
  CounterPreset #(.Bits(12)) PC (
    .en(1'b1), .C(PC_CK), .dir(1'b0), .in(PCIN), .ld(PC_LD), .clr(reset_1_out), .out(BUS_PC));  // open: ovf
  LED led_56 (.in(INST_TSF));
  LED led_57 (.in(OPR_CLA2));
  Switch #(.Closed("true")) HLT_ENABLED (.A(HALT), .B(HLT_ENABLED_b));
  Reset #(.invertOutput("false")) reset_1 (.out(reset_1_out));
  LED led_58 (.in(INST_TCF));
  LED led_59 (.in(OPR_SMA));
  LED led_60 (.in(NOIND));
  LED led_61 (.in(IND));
  RS_FF_AS rs_ff_as_2 (.S(monoflop_5_q), .R(or_13_out), .Q(rs_ff_as_2_q));  // open: nQ
  PullDown pulldown_24 (.out(HLT_ENABLED_b));
  Switch BP_ENABLED (.A(comparator_2_eq), .B(BP_ENABLED_b));
  // Probe on BUS_PC
  LED led_62 (.in(INST_TPC));
  LED led_63 (.in(INST_TSK));
  LED led_64 (.in(OPR_SZA));
  LED led_65 (.in(OPR_SNL));
  LED led_66 (.in(AUTOIND));
  or or_12 (or_12_out, monoflop_4_q, monoflop_5_q, rs_ff_as_2_q);
  or or_13 (or_13_out, H_out, BP_ENABLED_b, HLT_ENABLED_b);
  // OC12 oc12_2: pin names not known; wires that end beside it: BUS_PC, BUS_IR[6:0], BUS_PC[11:7], BUS_IR[7], IR2RAMA, {RA2[0], RA1, RA0}, {RA3, RA2[2:1]}
  LED led_67 (.in(IR2RAMA));
  LED led_68 (.in(INST_TLS));
  LED led_69 (.in(OPR_TSTINV));
  LED led_70 (.in(BUS_IR[7]));
  LED led_71 (.in(or_12_out));
  LED led_72 (.in(or_13_out));
  PullDown pulldown_25 (.out(BP_ENABLED_b));
  and and_21 (and_21_out, INST_TSF, FLAG_PRNRDY, PH04);
  and and_22 (HALT, OPR_HLT, PH02);
  LED led_73 (.in(PC2RAMA));
  assign {RA3, RA2, RA1, RA0} = PC2RAMA ? BUS_PC : 12'bz;  // Driver driver_12
  LED led_74 (.in(OPR_OSR));
  D_FF d_ff_1 (.D(PH12), .C(clk), .Q(d_ff_1_q));  // open: nQ
  LED led_75 (.in(and_21_out));
  LED led_76 (.in(HALT));
  // Probe on {RA3, RA2, RA1, RA0}
  LED led_77 (.in(OPR_HLT));
  LED led_78 (.in(OPR_NA1));
  assign IR_CK = and_21_out ? and_21_out : 1'bz;  // Driver driver_13
  assign PC_CK = and_21_out ? and_21_out : 1'bz;  // Driver driver_14
  Driver driver_15 (.in(and_21_out), .en(and_21_out));  // open: out
  Driver driver_16 (.in(and_21_out), .en(and_21_out));  // open: out
  Driver driver_17 (.in(and_21_out), .en(and_21_out));  // open: out
  LED led_79 (.in(IND2RAMA));
  assign {RA3, RA2, RA1, RA0} = IND2RAMA ? {IND3, IND2, IND1, IND0} : 12'bz;  // Driver driver_18
  LED led_80 (.in(OPR_NOP));
  RS_FF_AS rs_ff_as_3 (.S(or_12_out), .R(d_ff_1_q), .Q(rs_ff_as_3_q));  // open: nQ
  and and_23 (and_23_out, rs_ff_as_3_q, clk);
  LED led_81 (.in(and_23_out));
  EEPROM #(.AddrBits(12), .isProgramMemory("true"), .Bits(12)) eeprom_1 (
    .A({RA3, RA2, RA1, RA0}), .CS(1'b1), .WE(RAM_WE), .OE(RAM_OE), .D(RAMDATA));
  LED led_82 (.in(RAM_WE));
  LED led_83 (.in(RAM_OE));
  or or_14 (or_14_out, S_out, and_23_out);
  Counter #(.Bits(4)) counter_2 (.en(1'b1), .C(or_14_out), .clr(PH12), .out(counter_2_out));  // open: ovf
  LED led_84 (.in(or_14_out));
  // Probe on RAMDATA
  Seven_Seg_Hex seven_seg_hex_33 (.d(counter_2_out), .dp(1'b0));
  Decoder #(.Selector_Bits(4)) decoder_1 (
    .sel(counter_2_out), .out_0(PH00), .out_1(PH01), .out_2(PH02), .out_3(PH03), .out_4(PH04), .out_5(PH05),
    .out_6(PH06), .out_7(PH07), .out_8(PH08), .out_9(PH09), .out_10(PH10), .out_11(PH11), .out_12(PH12),
    .out_13(PH13), .out_14(PH14), .out_15(PH15));
  assign {DA3, DA2, DA1, DA0} = RAM_OE ? RAMDATA : 12'bz;  // Driver driver_19
  assign RAMDATA = RAM_WE ? {DA3, DA2, DA1, DA0} : 12'bz;  // Driver driver_20
  LED led_85 (.in(PC2RAMD));
  // Probe on {DA3, DA2, DA1, DA0}
  assign {DA3, DA2, DA1, DA0} = PC2RAMD ? BUS_PC : 12'bz;  // Driver driver_21
  D_FF #(.Bits(12)) IR (.D({DA3, DA2, DA1, DA0}), .C(IR_CK), .Q(BUS_IR));  // open: nQ
  LED led_86 (.in(IR_CK));
  LED led_87 (.in(INC2RAMD));
  assign {DA3, DA2, DA1, DA0} = INC2RAMD ? INC_s : 12'bz;  // Driver driver_22
  LED led_88 (.in(AC2RAMD));
  assign {DA3, DA2, DA1, DA0} = AC2RAMD ? AC : 12'bz;  // Driver driver_23
  // Probe on BUS_IR
  D_FF #(.Bits(12)) u_IND (.D({DA3, DA2, DA1, DA0}), .C(IND_CK), .Q({IND3, IND2, IND1, IND0}));  // open: nQ
  LED led_89 (.in(IND_CK));
  // Probe on {IND3, IND2, IND1, IND0}
  LED led_90 (.in(DATA_CK));
  D_FF #(.Bits(12)) DATA (.D({DA3, DA2, DA1, DA0}), .C(DATA_CK), .Q(LATCHEDDATA));  // open: nQ
  // Probe on LATCHEDDATA
  and and_24 (CNT_AND, AND, NOIND, PH02);
  LED led_91 (.in(CNT_AND));
  and and_25 (and_25_out, AND, NOIND, PH03);
  LED led_92 (.in(and_25_out));
  LED led_93 (.in(IND2INC));
  assign driver_24_out = IND2INC ? {IND3, IND2, IND1, IND0} : 12'bz;  // Driver driver_24
  LED led_94 (.in(LD2INC));
  assign driver_24_out = LD2INC ? LATCHEDDATA : 12'bz;  // Driver driver_25
  assign IR2RAMA = CNT_AND ? CNT_AND : 1'bz;  // Driver driver_26
  assign RAMD2AC_AND = CNT_AND ? CNT_AND : 1'bz;  // Driver driver_27
  assign RAM_OE = CNT_AND ? CNT_AND : 1'bz;  // Driver driver_28
  assign driver_29_out = CNT_AND ? CNT_AND : 1'bz;  // Driver driver_29
  assign driver_30_out = CNT_AND ? CNT_AND : 1'bz;  // Driver driver_30
  assign IR2RAMA = and_25_out ? and_25_out : 1'bz;  // Driver driver_31
  assign RAMD2AC_AND = and_25_out ? and_25_out : 1'bz;  // Driver driver_32
  assign RAM_OE = and_25_out ? and_25_out : 1'bz;  // Driver driver_33
  assign AC_CK = and_25_out ? and_25_out : 1'bz;  // Driver driver_34
  Driver driver_35 (.in(and_25_out), .en(and_25_out));  // open: out
  // Probe on driver_24_out
  // Probe on INC_s
  Add #(.Bits(12)) INC (.a({12{1'b0}}), .b(driver_24_out), .c_i(1'b1), .s(INC_s), .c_o(INCZERO));
  and and_26 (CNT_AND_I, AND, IND, PH02);
  and and_27 (and_27_out, AND, IND, PH03);
  and and_28 (and_28_out, AND, IND, PH04);
  and and_29 (and_29_out, AND, IND, PH05);
  Add #(.Bits(12)) add_1 (.a(AC), .b({DA3, DA2, DA1, DA0}), .c_i(1'b0), .s(add_1_s), .c_o(add_1_c_o));
  assign and_30_out = AC & {DA3, DA2, DA1, DA0};  // And and_30, 12 bits wide
  assign IR2RAMA = CNT_AND_I ? CNT_AND_I : 1'bz;  // Driver driver_36
  LED led_95 (.in(CNT_AND_I));
  assign RAMD2IND = CNT_AND_I ? CNT_AND_I : 1'bz;  // Driver driver_37
  assign RAM_OE = CNT_AND_I ? CNT_AND_I : 1'bz;  // Driver driver_38
  Driver driver_39 (.in(CNT_AND_I), .en(CNT_AND_I));  // open: out
  Driver driver_40 (.in(CNT_AND_I), .en(CNT_AND_I));  // open: out
  assign IR2RAMA = and_27_out ? and_27_out : 1'bz;  // Driver driver_41
  LED led_96 (.in(and_27_out));
  assign RAMD2IND = and_27_out ? and_27_out : 1'bz;  // Driver driver_42
  assign RAM_OE = and_27_out ? and_27_out : 1'bz;  // Driver driver_43
  assign IND_CK = and_27_out ? and_27_out : 1'bz;  // Driver driver_44
  Driver driver_45 (.in(and_27_out), .en(and_27_out));  // open: out
  assign IND2RAMA = and_28_out ? and_28_out : 1'bz;  // Driver driver_46
  LED led_97 (.in(and_28_out));
  assign RAMD2AC_AND = and_28_out ? and_28_out : 1'bz;  // Driver driver_47
  assign RAM_OE = and_28_out ? and_28_out : 1'bz;  // Driver driver_48
  Driver driver_49 (.in(and_28_out), .en(and_28_out));  // open: out
  Driver driver_50 (.in(and_28_out), .en(and_28_out));  // open: out
  assign IND2RAMA = and_29_out ? and_29_out : 1'bz;  // Driver driver_51
  LED led_98 (.in(and_29_out));
  assign RAMD2AC_AND = and_29_out ? and_29_out : 1'bz;  // Driver driver_52
  assign RAM_OE = and_29_out ? and_29_out : 1'bz;  // Driver driver_53
  assign AC_CK = and_29_out ? and_29_out : 1'bz;  // Driver driver_54
  Driver driver_55 (.in(and_29_out), .en(and_29_out));  // open: out
  // Probe on AC
  // Probe on add_1_s
  // Probe on and_30_out
  // Probe on rotater_1_p4
  and and_31 (and_31_out, add_1_c_o, RAMD2AC_ADD);
  xor xor_1 (xor_1_out, and_31_out, rotater_1_p5);
  assign driver_56_out = RAMD2AC_ADD ? add_1_s : 12'bz;  // Driver driver_56
  LED led_99 (.in(RAMD2AC_ADD));
  assign driver_56_out = RAMD2AC_AND ? and_30_out : 12'bz;  // Driver driver_57
  LED led_100 (.in(RAMD2AC_AND));
  assign driver_56_out = ROT2AC ? rotater_1_p4 : 12'bz;  // Driver driver_58
  LED led_101 (.in(ROT2AC));
  // Probe on driver_56_out
  D_FF u_LINK (.D(xor_1_out), .C(LINK_CK), .Q(LINK));  // open: nQ
  LED led_102 (.in(LINK_CK));
  and and_32 (CNT_AND_IA, AND, AUTOIND, PH02);
  and and_33 (and_33_out, AND, AUTOIND, PH03);
  and and_34 (and_34_out, AND, AUTOIND, PH04);
  and and_35 (and_35_out, AND, AUTOIND, PH05);
  and and_36 (and_36_out, AND, AUTOIND, PH06);
  and and_37 (and_37_out, AND, AUTOIND, PH07);
  and and_38 (and_38_out, AND, AUTOIND, PH08);
  D_FF #(.Bits(12)) u_AC (.D(driver_56_out), .C(AC_CK), .Q(AC));  // open: nQ
  LED led_103 (.in(AC_CK));
  LED led_104 (.in(CNT_AND_IA));
  LED led_105 (.in(and_33_out));
  LED led_106 (.in(and_34_out));
  LED led_107 (.in(and_35_out));
  LED led_108 (.in(and_36_out));
  LED led_109 (.in(and_37_out));
  LED led_110 (.in(and_38_out));
  assign IR2RAMA = CNT_AND_IA ? CNT_AND_IA : 1'bz;  // Driver driver_59
  assign RAM_OE = CNT_AND_IA ? CNT_AND_IA : 1'bz;  // Driver driver_60
  assign driver_61_out = CNT_AND_IA ? CNT_AND_IA : 1'bz;  // Driver driver_61
  assign driver_62_out = CNT_AND_IA ? CNT_AND_IA : 1'bz;  // Driver driver_62
  assign driver_63_out = CNT_AND_IA ? CNT_AND_IA : 1'bz;  // Driver driver_63
  assign IR2RAMA = and_33_out ? and_33_out : 1'bz;  // Driver driver_64
  assign IND_CK = and_33_out ? and_33_out : 1'bz;  // Driver driver_65
  assign RAM_OE = and_33_out ? and_33_out : 1'bz;  // Driver driver_66
  assign driver_67_out = and_33_out ? and_33_out : 1'bz;  // Driver driver_67
  assign driver_68_out = and_33_out ? and_33_out : 1'bz;  // Driver driver_68
  assign INC2RAMD = and_34_out ? and_34_out : 1'bz;  // Driver driver_69
  assign RAM_WE = and_34_out ? and_34_out : 1'bz;  // Driver driver_70
  assign IND2INC = and_34_out ? and_34_out : 1'bz;  // Driver driver_71
  assign driver_72_out = and_34_out ? and_34_out : 1'bz;  // Driver driver_72
  assign driver_73_out = and_34_out ? and_34_out : 1'bz;  // Driver driver_73
  assign IR2RAMA = and_35_out ? and_35_out : 1'bz;  // Driver driver_74
  assign RAMD2IND = and_35_out ? and_35_out : 1'bz;  // Driver driver_75
  assign RAM_OE = and_35_out ? and_35_out : 1'bz;  // Driver driver_76
  Driver driver_77 (.in(and_35_out), .en(and_35_out));  // open: out
  Driver driver_78 (.in(and_35_out), .en(and_35_out));  // open: out
  assign IR2RAMA = and_36_out ? and_36_out : 1'bz;  // Driver driver_79
  assign RAMD2IND = and_36_out ? and_36_out : 1'bz;  // Driver driver_80
  assign RAM_OE = and_36_out ? and_36_out : 1'bz;  // Driver driver_81
  assign IND_CK = and_36_out ? and_36_out : 1'bz;  // Driver driver_82
  Driver driver_83 (.in(and_36_out), .en(and_36_out));  // open: out
  assign IND2RAMA = and_37_out ? and_37_out : 1'bz;  // Driver driver_84
  assign RAMD2AC_AND = and_37_out ? and_37_out : 1'bz;  // Driver driver_85
  assign RAM_OE = and_37_out ? and_37_out : 1'bz;  // Driver driver_86
  Driver driver_87 (.in(and_37_out), .en(and_37_out));  // open: out
  Driver driver_88 (.in(and_37_out), .en(and_37_out));  // open: out
  assign IND2RAMA = and_38_out ? and_38_out : 1'bz;  // Driver driver_89
  assign RAMD2AC_AND = and_38_out ? and_38_out : 1'bz;  // Driver driver_90
  assign RAM_OE = and_38_out ? and_38_out : 1'bz;  // Driver driver_91
  assign AC_CK = and_38_out ? and_38_out : 1'bz;  // Driver driver_92
  Driver driver_93 (.in(and_38_out), .en(and_38_out));  // open: out
  // Probe on AC
  or or_15 (or_15_out, OPR_CLA2, OPR_CLA1, CLAx);
  assign and_39_out = AC & ~bitextender_1_out;  // And and_39, 12 bits wide
  BitExtender #(.inputBits(1), .outputBits(12)) bitextender_1 (.in(or_15_out), .out(bitextender_1_out));
  LED led_111 (.in(or_15_out));
  // Probe on and_39_out
  and and_40 (and_40_out, LINK, ~OPR_CLL);  // And
  LED led_112 (.in(OPR_CLL));
  DipSwitch dipswitch_1 (.out(dipswitch_1_out[11]));
  DipSwitch dipswitch_2 (.out(dipswitch_1_out[10]));
  DipSwitch dipswitch_3 (.out(dipswitch_1_out[9]));
  assign or_16_out = and_43_out | and_39_out;  // Or or_16, 12 bits wide
  LED led_113 (.in(and_40_out));
  DipSwitch dipswitch_4 (.out(dipswitch_1_out[8]));
  DipSwitch dipswitch_5 (.out(dipswitch_1_out[7]));
  DipSwitch dipswitch_6 (.out(dipswitch_1_out[6]));
  // Probe on or_16_out
  BitExtender #(.inputBits(1), .outputBits(12)) bitextender_2 (.in(OPR_CMA), .out(bitextender_2_out));
  xor xor_2 (xor_2_out, and_40_out, OPR_CML);
  LED led_114 (.in(OPR_CML));
  and and_41 (CNT_TAD, TAD, NOIND, PH02);
  and and_42 (and_42_out, TAD, NOIND, PH03);
  DipSwitch dipswitch_7 (.out(dipswitch_1_out[5]));
  DipSwitch dipswitch_8 (.out(dipswitch_1_out[4]));
  DipSwitch dipswitch_9 (.out(dipswitch_1_out[3]));
  assign and_43_out = bitextender_3_out & not_2_out;  // And and_43, 12 bits wide
  assign xor_3_out = or_16_out ^ bitextender_2_out;  // XOr xor_3, 12 bits wide
  LED led_115 (.in(xor_2_out));
  LED led_116 (.in(CNT_TAD));
  LED led_117 (.in(and_42_out));
  DipSwitch dipswitch_10 (.out(dipswitch_1_out[2]));
  DipSwitch dipswitch_11 (.out(dipswitch_1_out[1]));
  DipSwitch dipswitch_12 (.out(dipswitch_1_out[0]));
  assign not_2_out = ~dipswitch_1_out;  // Not not_2, 12 bits wide
  // Probe on not_2_out
  BitExtender #(.inputBits(1), .outputBits(12)) bitextender_3 (.in(OPR_OSR), .out(bitextender_3_out));
  // Probe on xor_3_out
  assign IR2RAMA = CNT_TAD ? CNT_TAD : 1'bz;  // Driver driver_94
  assign RAMD2AC_ADD = CNT_TAD ? CNT_TAD : 1'bz;  // Driver driver_95
  assign RAM_OE = CNT_TAD ? CNT_TAD : 1'bz;  // Driver driver_96
  assign driver_97_out = CNT_TAD ? CNT_TAD : 1'bz;  // Driver driver_97
  assign driver_98_out = CNT_TAD ? CNT_TAD : 1'bz;  // Driver driver_98
  assign IR2RAMA = and_42_out ? and_42_out : 1'bz;  // Driver driver_99
  assign RAMD2AC_ADD = and_42_out ? and_42_out : 1'bz;  // Driver driver_100
  assign RAM_OE = and_42_out ? and_42_out : 1'bz;  // Driver driver_101
  assign AC_CK = and_42_out ? and_42_out : 1'bz;  // Driver driver_102
  assign LINK_CK = and_42_out ? and_42_out : 1'bz;  // Driver driver_103
  Add #(.Bits(12)) add_2 (.a(xor_3_out), .b({12{1'b0}}), .c_i(OPR_IAC), .s(add_2_s), .c_o(add_2_c_o));
  // Probe on add_2_s
  or or_17 (or_17_out, add_2_c_o, and_40_out);
  LED led_118 (.in(or_17_out));
  // ROTATER rotater_1: pin names not known; wires that end beside it: {OPR_RIGHT, OPR_LEFT, OPR_X2}, add_2_s, rotater_1_p3, rotater_1_p4, rotater_1_p5
  xor xor_4 (rotater_1_p3, or_17_out, OPR_CML);
  LED led_119 (.in(rotater_1_p3));
  LED led_120 (.in(OPR_CML));
  and and_44 (CNT_TAD_I, TAD, IND, PH02);
  and and_45 (and_45_out, TAD, IND, PH03);
  and and_46 (and_46_out, TAD, IND, PH04);
  and and_47 (and_47_out, TAD, IND, PH05);
  // Probe on rotater_1_p4
  LED led_121 (.in(CNT_TAD_I));
  assign IR2RAMA = and_45_out ? and_45_out : 1'bz;  // Driver driver_104
  LED led_122 (.in(and_45_out));
  assign RAMD2IND = and_45_out ? and_45_out : 1'bz;  // Driver driver_105
  assign RAM_OE = and_45_out ? and_45_out : 1'bz;  // Driver driver_106
  assign IND_CK = and_45_out ? and_45_out : 1'bz;  // Driver driver_107
  Driver driver_108 (.in(and_45_out), .en(and_45_out));  // open: out
  assign IND2RAMA = and_46_out ? and_46_out : 1'bz;  // Driver driver_109
  LED led_123 (.in(and_46_out));
  assign RAMD2AC_ADD = and_46_out ? and_46_out : 1'bz;  // Driver driver_110
  assign RAM_OE = and_46_out ? and_46_out : 1'bz;  // Driver driver_111
  Driver driver_112 (.in(and_46_out), .en(and_46_out));  // open: out
  Driver driver_113 (.in(and_46_out), .en(and_46_out));  // open: out
  assign IND2RAMA = and_47_out ? and_47_out : 1'bz;  // Driver driver_114
  LED led_124 (.in(and_47_out));
  assign RAMD2AC_ADD = and_47_out ? and_47_out : 1'bz;  // Driver driver_115
  assign RAM_OE = and_47_out ? and_47_out : 1'bz;  // Driver driver_116
  assign AC_CK = and_47_out ? and_47_out : 1'bz;  // Driver driver_117
  assign LINK_CK = and_47_out ? and_47_out : 1'bz;  // Driver driver_118
  assign IR2RAMA = CNT_TAD_I ? CNT_TAD_I : 1'bz;  // Driver driver_119
  assign RAMD2IND = CNT_TAD_I ? CNT_TAD_I : 1'bz;  // Driver driver_120
  assign RAM_OE = CNT_TAD_I ? CNT_TAD_I : 1'bz;  // Driver driver_121
  Driver driver_122 (.in(CNT_TAD_I), .en(CNT_TAD_I));  // open: out
  Driver driver_123 (.in(CNT_TAD_I), .en(CNT_TAD_I));  // open: out
  nor nor_2 (nor_2_out, AC[0], AC[1], AC[2], AC[3], AC[4], AC[5], AC[6], AC[7], AC[8], AC[9], AC[10], AC[11]);
  LED led_125 (.in(nor_2_out));
  and and_48 (CNT_TAD_IA, TAD, AUTOIND, PH02);
  and and_49 (and_49_out, TAD, AUTOIND, PH03);
  and and_50 (and_50_out, TAD, AUTOIND, PH04);
  and and_51 (and_51_out, TAD, AUTOIND, PH05);
  and and_52 (and_52_out, TAD, AUTOIND, PH06);
  LED led_126 (.in(and_52_out));
  and and_53 (and_53_out, TAD, AUTOIND, PH07);
  LED led_127 (.in(and_53_out));
  and and_54 (and_54_out, TAD, AUTOIND, PH08);
  LED led_128 (.in(and_54_out));
  and and_55 (and_55_out, nor_2_out, OPR_SZA);
  and and_56 (and_56_out, AC[11], OPR_SMA);
  and and_57 (and_57_out, OPR_SNL, LINK);
  assign IR2RAMA = CNT_TAD_IA ? CNT_TAD_IA : 1'bz;  // Driver driver_124
  LED led_129 (.in(CNT_TAD_IA));
  assign RAM_OE = CNT_TAD_IA ? CNT_TAD_IA : 1'bz;  // Driver driver_125
  Driver driver_126 (.in(CNT_TAD_IA), .en(CNT_TAD_IA));  // open: out
  Driver driver_127 (.in(CNT_TAD_IA), .en(CNT_TAD_IA));  // open: out
  Driver driver_128 (.in(CNT_TAD_IA), .en(CNT_TAD_IA));  // open: out
  assign IR2RAMA = and_49_out ? and_49_out : 1'bz;  // Driver driver_129
  LED led_130 (.in(and_49_out));
  assign IND_CK = and_49_out ? and_49_out : 1'bz;  // Driver driver_130
  assign RAM_OE = and_49_out ? and_49_out : 1'bz;  // Driver driver_131
  Driver driver_132 (.in(and_49_out), .en(and_49_out));  // open: out
  Driver driver_133 (.in(and_49_out), .en(and_49_out));  // open: out
  assign INC2RAMD = and_50_out ? and_50_out : 1'bz;  // Driver driver_134
  LED led_131 (.in(and_50_out));
  assign RAM_WE = and_50_out ? and_50_out : 1'bz;  // Driver driver_135
  assign IND2INC = and_50_out ? and_50_out : 1'bz;  // Driver driver_136
  Driver driver_137 (.in(and_50_out), .en(and_50_out));  // open: out
  Driver driver_138 (.in(and_50_out), .en(and_50_out));  // open: out
  assign IR2RAMA = and_51_out ? and_51_out : 1'bz;  // Driver driver_139
  LED led_132 (.in(and_51_out));
  assign RAMD2IND = and_51_out ? and_51_out : 1'bz;  // Driver driver_140
  assign RAM_OE = and_51_out ? and_51_out : 1'bz;  // Driver driver_141
  Driver driver_142 (.in(and_51_out), .en(and_51_out));  // open: out
  Driver driver_143 (.in(and_51_out), .en(and_51_out));  // open: out
  assign IR2RAMA = and_52_out ? and_52_out : 1'bz;  // Driver driver_144
  assign RAMD2IND = and_52_out ? and_52_out : 1'bz;  // Driver driver_145
  assign RAM_OE = and_52_out ? and_52_out : 1'bz;  // Driver driver_146
  assign IND_CK = and_52_out ? and_52_out : 1'bz;  // Driver driver_147
  Driver driver_148 (.in(and_52_out), .en(and_52_out));  // open: out
  assign IND2RAMA = and_53_out ? and_53_out : 1'bz;  // Driver driver_149
  assign RAMD2AC_ADD = and_53_out ? and_53_out : 1'bz;  // Driver driver_150
  assign RAM_OE = and_53_out ? and_53_out : 1'bz;  // Driver driver_151
  Driver driver_152 (.in(and_53_out), .en(and_53_out));  // open: out
  Driver driver_153 (.in(and_53_out), .en(and_53_out));  // open: out
  assign IND2RAMA = and_54_out ? and_54_out : 1'bz;  // Driver driver_154
  assign RAMD2AC_ADD = and_54_out ? and_54_out : 1'bz;  // Driver driver_155
  assign RAM_OE = and_54_out ? and_54_out : 1'bz;  // Driver driver_156
  assign AC_CK = and_54_out ? and_54_out : 1'bz;  // Driver driver_157
  assign LINK_CK = and_54_out ? and_54_out : 1'bz;  // Driver driver_158
  LED led_133 (.in(and_55_out));
  LED led_134 (.in(and_56_out));
  LED led_135 (.in(and_57_out));
  or or_18 (or_18_out, and_55_out, and_56_out, and_57_out);
  LED led_136 (.in(or_18_out));
  xor xor_5 (SKIP, or_18_out, OPR_TSTINV);
  LED led_137 (.in(SKIP));
  and and_58 (CNT_ISZ, ISZ, NOIND, PH02);
  and and_59 (and_59_out, ISZ, NOIND, PH03);
  and and_60 (and_60_out, ISZ, NOIND, PH04);
  and and_61 (and_61_out, ISZ, NOIND, PH05);
  and and_62 (and_62_out, ISZ, NOIND, INCZERO, PH06);
  LED led_138 (.in(CNT_ISZ));
  LED led_139 (.in(and_59_out));
  LED led_140 (.in(and_60_out));
  LED led_141 (.in(and_61_out));
  LED led_142 (.in(and_62_out));
  assign IR2RAMA = CNT_ISZ ? CNT_ISZ : 1'bz;  // Driver driver_159
  assign RAM_OE = CNT_ISZ ? CNT_ISZ : 1'bz;  // Driver driver_160
  Driver driver_161 (.in(CNT_ISZ), .en(CNT_ISZ));  // open: out
  Driver driver_162 (.in(CNT_ISZ), .en(CNT_ISZ));  // open: out
  Driver driver_163 (.in(CNT_ISZ), .en(CNT_ISZ));  // open: out
  assign IR2RAMA = and_59_out ? and_59_out : 1'bz;  // Driver driver_164
  assign RAM_OE = and_59_out ? and_59_out : 1'bz;  // Driver driver_165
  assign DATA_CK = and_59_out ? and_59_out : 1'bz;  // Driver driver_166
  assign LD2INC = and_59_out ? and_59_out : 1'bz;  // Driver driver_167
  Driver driver_168 (.in(and_59_out), .en(and_59_out));  // open: out
  assign IR2RAMA = and_60_out ? and_60_out : 1'bz;  // Driver driver_169
  assign RAM_WE = and_60_out ? and_60_out : 1'bz;  // Driver driver_170
  assign INC2RAMD = and_60_out ? and_60_out : 1'bz;  // Driver driver_171
  assign LD2INC = and_60_out ? and_60_out : 1'bz;  // Driver driver_172
  Driver driver_173 (.in(and_60_out), .en(and_60_out));  // open: out
  assign IR2RAMA = and_61_out ? and_61_out : 1'bz;  // Driver driver_174
  assign RAM_OE = and_61_out ? and_61_out : 1'bz;  // Driver driver_175
  assign LD2INC = and_61_out ? and_61_out : 1'bz;  // Driver driver_176
  Driver driver_177 (.in(and_61_out), .en(and_61_out));  // open: out
  Driver driver_178 (.in(and_61_out), .en(and_61_out));  // open: out
  assign PC_CK = and_62_out ? and_62_out : 1'bz;  // Driver driver_179
  assign LD2INC = and_62_out ? and_62_out : 1'bz;  // Driver driver_180
  Driver driver_181 (.in(and_62_out), .en(and_62_out));  // open: out
  Driver driver_182 (.in(and_62_out), .en(and_62_out));  // open: out
  Driver driver_183 (.in(and_62_out), .en(and_62_out));  // open: out
  and and_63 (CNT_ISZ_I, ISZ, IND, PH02);
  LED led_143 (.in(CNT_ISZ_I));
  and and_64 (and_64_out, ISZ, IND, PH03);
  LED led_144 (.in(and_64_out));
  and and_65 (and_65_out, ISZ, IND, PH04);
  LED led_145 (.in(and_65_out));
  and and_66 (and_66_out, ISZ, IND, PH05);
  LED led_146 (.in(and_66_out));
  and and_67 (and_67_out, ISZ, IND, PH06);
  LED led_147 (.in(and_67_out));
  and and_68 (and_68_out, ISZ, IND, PH07);
  LED led_148 (.in(and_68_out));
  and and_69 (and_69_out, ISZ, IND, INCZERO, PH08);
  LED led_149 (.in(and_69_out));
  assign IR2RAMA = CNT_ISZ_I ? CNT_ISZ_I : 1'bz;  // Driver driver_184
  assign RAMD2IND = CNT_ISZ_I ? CNT_ISZ_I : 1'bz;  // Driver driver_185
  assign RAM_OE = CNT_ISZ_I ? CNT_ISZ_I : 1'bz;  // Driver driver_186
  Driver driver_187 (.in(CNT_ISZ_I), .en(CNT_ISZ_I));  // open: out
  Driver driver_188 (.in(CNT_ISZ_I), .en(CNT_ISZ_I));  // open: out
  assign IR2RAMA = and_64_out ? and_64_out : 1'bz;  // Driver driver_189
  assign RAMD2IND = and_64_out ? and_64_out : 1'bz;  // Driver driver_190
  assign RAM_OE = and_64_out ? and_64_out : 1'bz;  // Driver driver_191
  assign IND_CK = and_64_out ? and_64_out : 1'bz;  // Driver driver_192
  Driver driver_193 (.in(and_64_out), .en(and_64_out));  // open: out
  assign IND2RAMA = and_65_out ? and_65_out : 1'bz;  // Driver driver_194
  assign RAM_OE = and_65_out ? and_65_out : 1'bz;  // Driver driver_195
  Driver driver_196 (.in(and_65_out), .en(and_65_out));  // open: out
  Driver driver_197 (.in(and_65_out), .en(and_65_out));  // open: out
  Driver driver_198 (.in(and_65_out), .en(and_65_out));  // open: out
  assign IND2RAMA = and_66_out ? and_66_out : 1'bz;  // Driver driver_199
  assign RAM_OE = and_66_out ? and_66_out : 1'bz;  // Driver driver_200
  assign DATA_CK = and_66_out ? and_66_out : 1'bz;  // Driver driver_201
  assign LD2INC = and_66_out ? and_66_out : 1'bz;  // Driver driver_202
  Driver driver_203 (.in(and_66_out), .en(and_66_out));  // open: out
  assign IND2RAMA = and_67_out ? and_67_out : 1'bz;  // Driver driver_204
  assign RAM_WE = and_67_out ? and_67_out : 1'bz;  // Driver driver_205
  assign INC2RAMD = and_67_out ? and_67_out : 1'bz;  // Driver driver_206
  assign LD2INC = and_67_out ? and_67_out : 1'bz;  // Driver driver_207
  Driver driver_208 (.in(and_67_out), .en(and_67_out));  // open: out
  assign IND2RAMA = and_68_out ? and_68_out : 1'bz;  // Driver driver_209
  assign RAM_OE = and_68_out ? and_68_out : 1'bz;  // Driver driver_210
  assign LD2INC = and_68_out ? and_68_out : 1'bz;  // Driver driver_211
  Driver driver_212 (.in(and_68_out), .en(and_68_out));  // open: out
  Driver driver_213 (.in(and_68_out), .en(and_68_out));  // open: out
  assign PC_CK = and_69_out ? and_69_out : 1'bz;  // Driver driver_214
  assign LD2INC = and_69_out ? and_69_out : 1'bz;  // Driver driver_215
  Driver driver_216 (.in(and_69_out), .en(and_69_out));  // open: out
  Driver driver_217 (.in(and_69_out), .en(and_69_out));  // open: out
  Driver driver_218 (.in(and_69_out), .en(and_69_out));  // open: out
  and and_70 (CNT_ISZ_IA, ISZ, AUTOIND, PH02);
  and and_71 (and_71_out, ISZ, AUTOIND, PH03);
  and and_72 (and_72_out, ISZ, AUTOIND, PH04);
  and and_73 (and_73_out, ISZ, AUTOIND, PH05);
  and and_74 (and_74_out, ISZ, AUTOIND, PH06);
  and and_75 (and_75_out, ISZ, AUTOIND, PH07);
  and and_76 (and_76_out, ISZ, AUTOIND, PH08);
  and and_77 (and_77_out, ISZ, AUTOIND, PH09);
  and and_78 (and_78_out, ISZ, AUTOIND, PH10);
  and and_79 (and_79_out, ISZ, AUTOIND, INCZERO, PH11);
  LED led_150 (.in(CNT_ISZ_IA));
  LED led_151 (.in(and_71_out));
  LED led_152 (.in(and_72_out));
  LED led_153 (.in(and_73_out));
  LED led_154 (.in(and_74_out));
  LED led_155 (.in(and_75_out));
  LED led_156 (.in(and_76_out));
  assign IND2RAMA = and_77_out ? and_77_out : 1'bz;  // Driver driver_219
  LED led_157 (.in(and_77_out));
  assign RAM_WE = and_77_out ? and_77_out : 1'bz;  // Driver driver_220
  assign INC2RAMD = and_77_out ? and_77_out : 1'bz;  // Driver driver_221
  assign LD2INC = and_77_out ? and_77_out : 1'bz;  // Driver driver_222
  Driver driver_223 (.in(and_77_out), .en(and_77_out));  // open: out
  assign IND2RAMA = and_78_out ? and_78_out : 1'bz;  // Driver driver_224
  LED led_158 (.in(and_78_out));
  assign RAM_OE = and_78_out ? and_78_out : 1'bz;  // Driver driver_225
  assign LD2INC = and_78_out ? and_78_out : 1'bz;  // Driver driver_226
  Driver driver_227 (.in(and_78_out), .en(and_78_out));  // open: out
  Driver driver_228 (.in(and_78_out), .en(and_78_out));  // open: out
  assign PC_CK = and_79_out ? and_79_out : 1'bz;  // Driver driver_229
  LED led_159 (.in(and_79_out));
  assign LD2INC = and_79_out ? and_79_out : 1'bz;  // Driver driver_230
  Driver driver_231 (.in(and_79_out), .en(and_79_out));  // open: out
  Driver driver_232 (.in(and_79_out), .en(and_79_out));  // open: out
  Driver driver_233 (.in(and_79_out), .en(and_79_out));  // open: out
  assign IR2RAMA = CNT_ISZ_IA ? CNT_ISZ_IA : 1'bz;  // Driver driver_234
  assign RAM_OE = CNT_ISZ_IA ? CNT_ISZ_IA : 1'bz;  // Driver driver_235
  Driver driver_236 (.in(CNT_ISZ_IA), .en(CNT_ISZ_IA));  // open: out
  Driver driver_237 (.in(CNT_ISZ_IA), .en(CNT_ISZ_IA));  // open: out
  Driver driver_238 (.in(CNT_ISZ_IA), .en(CNT_ISZ_IA));  // open: out
  assign IR2RAMA = and_71_out ? and_71_out : 1'bz;  // Driver driver_239
  assign IND_CK = and_71_out ? and_71_out : 1'bz;  // Driver driver_240
  assign RAM_OE = and_71_out ? and_71_out : 1'bz;  // Driver driver_241
  Driver driver_242 (.in(and_71_out), .en(and_71_out));  // open: out
  Driver driver_243 (.in(and_71_out), .en(and_71_out));  // open: out
  assign INC2RAMD = and_72_out ? and_72_out : 1'bz;  // Driver driver_244
  assign RAM_WE = and_72_out ? and_72_out : 1'bz;  // Driver driver_245
  assign IND2INC = and_72_out ? and_72_out : 1'bz;  // Driver driver_246
  Driver driver_247 (.in(and_72_out), .en(and_72_out));  // open: out
  Driver driver_248 (.in(and_72_out), .en(and_72_out));  // open: out
  assign IR2RAMA = and_73_out ? and_73_out : 1'bz;  // Driver driver_249
  assign RAMD2IND = and_73_out ? and_73_out : 1'bz;  // Driver driver_250
  assign RAM_OE = and_73_out ? and_73_out : 1'bz;  // Driver driver_251
  Driver driver_252 (.in(and_73_out), .en(and_73_out));  // open: out
  Driver driver_253 (.in(and_73_out), .en(and_73_out));  // open: out
  assign IR2RAMA = and_74_out ? and_74_out : 1'bz;  // Driver driver_254
  assign RAMD2IND = and_74_out ? and_74_out : 1'bz;  // Driver driver_255
  assign RAM_OE = and_74_out ? and_74_out : 1'bz;  // Driver driver_256
  assign IND_CK = and_74_out ? and_74_out : 1'bz;  // Driver driver_257
  Driver driver_258 (.in(and_74_out), .en(and_74_out));  // open: out
  assign IND2RAMA = and_75_out ? and_75_out : 1'bz;  // Driver driver_259
  assign RAM_OE = and_75_out ? and_75_out : 1'bz;  // Driver driver_260
  Driver driver_261 (.in(and_75_out), .en(and_75_out));  // open: out
  Driver driver_262 (.in(and_75_out), .en(and_75_out));  // open: out
  Driver driver_263 (.in(and_75_out), .en(and_75_out));  // open: out
  assign IND2RAMA = and_76_out ? and_76_out : 1'bz;  // Driver driver_264
  assign RAM_OE = and_76_out ? and_76_out : 1'bz;  // Driver driver_265
  assign DATA_CK = and_76_out ? and_76_out : 1'bz;  // Driver driver_266
  assign LD2INC = and_76_out ? and_76_out : 1'bz;  // Driver driver_267
  Driver driver_268 (.in(and_76_out), .en(and_76_out));  // open: out
  and and_80 (CNT_DCA, DCA, NOIND, PH02);
  LED led_160 (.in(CNT_DCA));
  and and_81 (and_81_out, DCA, NOIND, PH03);
  LED led_161 (.in(and_81_out));
  and and_82 (and_82_out, DCA, NOIND, PH04);
  LED led_162 (.in(and_82_out));
  assign IR2RAMA = CNT_DCA ? CNT_DCA : 1'bz;  // Driver driver_269
  assign AC2RAMD = CNT_DCA ? CNT_DCA : 1'bz;  // Driver driver_270
  Driver driver_271 (.in(CNT_DCA), .en(CNT_DCA));  // open: out
  Driver driver_272 (.in(CNT_DCA), .en(CNT_DCA));  // open: out
  Driver driver_273 (.in(CNT_DCA), .en(CNT_DCA));  // open: out
  assign IR2RAMA = and_81_out ? and_81_out : 1'bz;  // Driver driver_274
  assign AC2RAMD = and_81_out ? and_81_out : 1'bz;  // Driver driver_275
  assign RAM_WE = and_81_out ? and_81_out : 1'bz;  // Driver driver_276
  assign CLA = and_81_out ? and_81_out : 1'bz;  // Driver driver_277
  Driver driver_278 (.in(and_81_out), .en(and_81_out));  // open: out
  assign CLAx = and_82_out ? and_82_out : 1'bz;  // Driver driver_279
  assign ROT2AC = and_82_out ? and_82_out : 1'bz;  // Driver driver_280
  assign AC_CK = and_82_out ? and_82_out : 1'bz;  // Driver driver_281
  Driver driver_282 (.in(and_82_out), .en(and_82_out));  // open: out
  Driver driver_283 (.in(and_82_out), .en(and_82_out));  // open: out
  and and_83 (CNT_DCA_I, DCA, IND, PH02);
  and and_84 (and_84_out, DCA, IND, PH03);
  and and_85 (and_85_out, DCA, IND, PH04);
  and and_86 (and_86_out, DCA, IND, PH05);
  and and_87 (and_87_out, DCA, IND, PH06);
  LED led_163 (.in(CNT_DCA_I));
  LED led_164 (.in(and_84_out));
  LED led_165 (.in(and_85_out));
  LED led_166 (.in(and_86_out));
  LED led_167 (.in(and_87_out));
  assign IR2RAMA = CNT_DCA_I ? CNT_DCA_I : 1'bz;  // Driver driver_284
  assign RAMD2IND = CNT_DCA_I ? CNT_DCA_I : 1'bz;  // Driver driver_285
  assign RAM_OE = CNT_DCA_I ? CNT_DCA_I : 1'bz;  // Driver driver_286
  assign driver_287_out = CNT_DCA_I ? CNT_DCA_I : 1'bz;  // Driver driver_287
  assign driver_288_out = CNT_DCA_I ? CNT_DCA_I : 1'bz;  // Driver driver_288
  assign IR2RAMA = and_84_out ? and_84_out : 1'bz;  // Driver driver_289
  assign RAMD2IND = and_84_out ? and_84_out : 1'bz;  // Driver driver_290
  assign RAM_OE = and_84_out ? and_84_out : 1'bz;  // Driver driver_291
  assign IND_CK = and_84_out ? and_84_out : 1'bz;  // Driver driver_292
  assign driver_293_out = and_84_out ? and_84_out : 1'bz;  // Driver driver_293
  assign IND2RAMA = and_85_out ? and_85_out : 1'bz;  // Driver driver_294
  assign AC2RAMD = and_85_out ? and_85_out : 1'bz;  // Driver driver_295
  Driver driver_296 (.in(and_85_out), .en(and_85_out));  // open: out
  Driver driver_297 (.in(and_85_out), .en(and_85_out));  // open: out
  Driver driver_298 (.in(and_85_out), .en(and_85_out));  // open: out
  assign IND2RAMA = and_86_out ? and_86_out : 1'bz;  // Driver driver_299
  assign AC2RAMD = and_86_out ? and_86_out : 1'bz;  // Driver driver_300
  assign RAM_WE = and_86_out ? and_86_out : 1'bz;  // Driver driver_301
  assign CLA = and_86_out ? and_86_out : 1'bz;  // Driver driver_302
  Driver driver_303 (.in(and_86_out), .en(and_86_out));  // open: out
  assign CLAx = and_87_out ? and_87_out : 1'bz;  // Driver driver_304
  assign ROT2AC = and_87_out ? and_87_out : 1'bz;  // Driver driver_305
  assign AC_CK = and_87_out ? and_87_out : 1'bz;  // Driver driver_306
  Driver driver_307 (.in(and_87_out), .en(and_87_out));  // open: out
  Driver driver_308 (.in(and_87_out), .en(and_87_out));  // open: out
  and and_88 (CNT_DCA_IA, DCA, AUTOIND, PH02);
  and and_89 (and_89_out, DCA, AUTOIND, PH03);
  and and_90 (and_90_out, DCA, AUTOIND, PH04);
  and and_91 (and_91_out, DCA, AUTOIND, PH05);
  and and_92 (and_92_out, DCA, AUTOIND, PH06);
  assign IR2RAMA = CNT_DCA_IA ? CNT_DCA_IA : 1'bz;  // Driver driver_309
  LED led_168 (.in(CNT_DCA_IA));
  assign RAM_OE = CNT_DCA_IA ? CNT_DCA_IA : 1'bz;  // Driver driver_310
  assign driver_311_out = CNT_DCA_IA ? CNT_DCA_IA : 1'bz;  // Driver driver_311
  assign driver_312_out = CNT_DCA_IA ? CNT_DCA_IA : 1'bz;  // Driver driver_312
  assign driver_313_out = CNT_DCA_IA ? CNT_DCA_IA : 1'bz;  // Driver driver_313
  assign IR2RAMA = and_89_out ? and_89_out : 1'bz;  // Driver driver_314
  LED led_169 (.in(and_89_out));
  assign IND_CK = and_89_out ? and_89_out : 1'bz;  // Driver driver_315
  assign RAM_OE = and_89_out ? and_89_out : 1'bz;  // Driver driver_316
  assign driver_317_out = and_89_out ? and_89_out : 1'bz;  // Driver driver_317
  assign driver_318_out = and_89_out ? and_89_out : 1'bz;  // Driver driver_318
  assign INC2RAMD = and_90_out ? and_90_out : 1'bz;  // Driver driver_319
  LED led_170 (.in(and_90_out));
  assign RAM_WE = and_90_out ? and_90_out : 1'bz;  // Driver driver_320
  assign IND2INC = and_90_out ? and_90_out : 1'bz;  // Driver driver_321
  assign driver_322_out = and_90_out ? and_90_out : 1'bz;  // Driver driver_322
  assign driver_323_out = and_90_out ? and_90_out : 1'bz;  // Driver driver_323
  assign IR2RAMA = and_91_out ? and_91_out : 1'bz;  // Driver driver_324
  LED led_171 (.in(and_91_out));
  assign RAMD2IND = and_91_out ? and_91_out : 1'bz;  // Driver driver_325
  assign RAM_OE = and_91_out ? and_91_out : 1'bz;  // Driver driver_326
  assign driver_327_out = and_91_out ? and_91_out : 1'bz;  // Driver driver_327
  assign driver_328_out = and_91_out ? and_91_out : 1'bz;  // Driver driver_328
  assign IR2RAMA = and_92_out ? and_92_out : 1'bz;  // Driver driver_329
  LED led_172 (.in(and_92_out));
  assign RAMD2IND = and_92_out ? and_92_out : 1'bz;  // Driver driver_330
  assign RAM_OE = and_92_out ? and_92_out : 1'bz;  // Driver driver_331
  assign IND_CK = and_92_out ? and_92_out : 1'bz;  // Driver driver_332
  assign driver_333_out = and_92_out ? and_92_out : 1'bz;  // Driver driver_333
  and and_93 (CNT_JMS, JMS, NOIND, PH02);
  and and_94 (and_94_out, JMS, NOIND, PH03);
  and and_95 (and_95_out, JMS, NOIND, PH04);
  and and_96 (and_96_out, JMS, NOIND, PH05);
  and and_97 (and_97_out, JMS, NOIND, PH06);
  LED led_173 (.in(CNT_JMS));
  assign PC2RAMD = and_94_out ? and_94_out : 1'bz;  // Driver driver_334
  LED led_174 (.in(and_94_out));
  assign IR2RAMA = and_94_out ? and_94_out : 1'bz;  // Driver driver_335
  assign RAM_WE = and_94_out ? and_94_out : 1'bz;  // Driver driver_336
  assign IR2PC = and_94_out ? and_94_out : 1'bz;  // Driver driver_337
  assign driver_338_out = and_94_out ? and_94_out : 1'bz;  // Driver driver_338
  LED led_175 (.in(and_95_out));
  LED led_176 (.in(and_96_out));
  LED led_177 (.in(and_97_out));
  assign PC2RAMD = CNT_JMS ? CNT_JMS : 1'bz;  // Driver driver_339
  assign IR2RAMA = CNT_JMS ? CNT_JMS : 1'bz;  // Driver driver_340
  assign driver_341_out = CNT_JMS ? CNT_JMS : 1'bz;  // Driver driver_341
  assign driver_342_out = CNT_JMS ? CNT_JMS : 1'bz;  // Driver driver_342
  assign driver_343_out = CNT_JMS ? CNT_JMS : 1'bz;  // Driver driver_343
  assign IR2PC = and_95_out ? and_95_out : 1'bz;  // Driver driver_344
  assign PC_LD = and_95_out ? and_95_out : 1'bz;  // Driver driver_345
  assign PC_CK = and_95_out ? and_95_out : 1'bz;  // Driver driver_346
  assign driver_347_out = and_95_out ? and_95_out : 1'bz;  // Driver driver_347
  assign driver_348_out = and_95_out ? and_95_out : 1'bz;  // Driver driver_348
  assign driver_349_out = and_96_out ? and_96_out : 1'bz;  // Driver driver_349
  assign driver_350_out = and_96_out ? and_96_out : 1'bz;  // Driver driver_350
  assign driver_351_out = and_96_out ? and_96_out : 1'bz;  // Driver driver_351
  assign driver_352_out = and_96_out ? and_96_out : 1'bz;  // Driver driver_352
  assign driver_353_out = and_96_out ? and_96_out : 1'bz;  // Driver driver_353
  assign PC_CK = and_97_out ? and_97_out : 1'bz;  // Driver driver_354
  assign driver_355_out = and_97_out ? and_97_out : 1'bz;  // Driver driver_355
  assign driver_356_out = and_97_out ? and_97_out : 1'bz;  // Driver driver_356
  assign driver_357_out = and_97_out ? and_97_out : 1'bz;  // Driver driver_357
  Driver driver_358 (.in(and_97_out), .en(and_97_out));  // open: out
  and and_98 (CNT_JMS_I, JMS, IND, PH02);
  and and_99 (and_99_out, JMS, IND, PH03);
  and and_100 (and_100_out, JMS, IND, PH04);
  and and_101 (and_101_out, JMS, IND, PH05);
  and and_102 (and_102_out, JMS, IND, PH06);
  and and_103 (and_103_out, JMS, IND, PH07);
  and and_104 (and_104_out, JMS, IND, PH08);
  LED led_178 (.in(CNT_JMS_I));
  LED led_179 (.in(and_99_out));
  LED led_180 (.in(and_100_out));
  LED led_181 (.in(and_101_out));
  LED led_182 (.in(and_102_out));
  LED led_183 (.in(and_103_out));
  LED led_184 (.in(and_104_out));
  assign IR2RAMA = CNT_JMS_I ? CNT_JMS_I : 1'bz;  // Driver driver_359
  assign RAMD2IND = CNT_JMS_I ? CNT_JMS_I : 1'bz;  // Driver driver_360
  assign RAM_OE = CNT_JMS_I ? CNT_JMS_I : 1'bz;  // Driver driver_361
  assign driver_362_out = CNT_JMS_I ? CNT_JMS_I : 1'bz;  // Driver driver_362
  assign driver_363_out = CNT_JMS_I ? CNT_JMS_I : 1'bz;  // Driver driver_363
  assign IR2RAMA = and_99_out ? and_99_out : 1'bz;  // Driver driver_364
  assign RAMD2IND = and_99_out ? and_99_out : 1'bz;  // Driver driver_365
  assign RAM_OE = and_99_out ? and_99_out : 1'bz;  // Driver driver_366
  assign IND_CK = and_99_out ? and_99_out : 1'bz;  // Driver driver_367
  assign driver_368_out = and_99_out ? and_99_out : 1'bz;  // Driver driver_368
  assign IND2RAMA = and_100_out ? and_100_out : 1'bz;  // Driver driver_369
  assign PC2RAMD = and_100_out ? and_100_out : 1'bz;  // Driver driver_370
  Driver driver_371 (.in(and_100_out), .en(and_100_out));  // open: out
  assign driver_372_out = and_100_out ? and_100_out : 1'bz;  // Driver driver_372
  assign driver_373_out = and_100_out ? and_100_out : 1'bz;  // Driver driver_373
  assign IND2RAMA = and_101_out ? and_101_out : 1'bz;  // Driver driver_374
  assign PC2RAMD = and_101_out ? and_101_out : 1'bz;  // Driver driver_375
  assign RAM_WE = and_101_out ? and_101_out : 1'bz;  // Driver driver_376
  assign PC_LD = and_101_out ? and_101_out : 1'bz;  // Driver driver_377
  assign IND2PC = and_101_out ? and_101_out : 1'bz;  // Driver driver_378
  assign IND2PC = and_102_out ? and_102_out : 1'bz;  // Driver driver_379
  assign PC_LD = and_102_out ? and_102_out : 1'bz;  // Driver driver_380
  assign PC_CK = and_102_out ? and_102_out : 1'bz;  // Driver driver_381
  Driver driver_382 (.in(and_102_out), .en(and_102_out));  // open: out
  assign driver_383_out = and_102_out ? and_102_out : 1'bz;  // Driver driver_383
  Driver driver_384 (.in(and_103_out), .en(and_103_out));  // open: out
  Driver driver_385 (.in(and_103_out), .en(and_103_out));  // open: out
  assign driver_386_out = and_103_out ? and_103_out : 1'bz;  // Driver driver_386
  assign driver_387_out = and_103_out ? and_103_out : 1'bz;  // Driver driver_387
  assign driver_388_out = and_103_out ? and_103_out : 1'bz;  // Driver driver_388
  assign PC_CK = and_104_out ? and_104_out : 1'bz;  // Driver driver_389
  assign driver_390_out = and_104_out ? and_104_out : 1'bz;  // Driver driver_390
  assign driver_391_out = and_104_out ? and_104_out : 1'bz;  // Driver driver_391
  assign driver_392_out = and_104_out ? and_104_out : 1'bz;  // Driver driver_392
  Driver driver_393 (.in(and_104_out), .en(and_104_out));  // open: out
  and and_105 (CNT_JMS_IA, JMS, AUTOIND, PH02);
  and and_106 (and_106_out, JMS, AUTOIND, PH03);
  and and_107 (and_107_out, JMS, AUTOIND, PH04);
  and and_108 (and_108_out, JMS, AUTOIND, PH05);
  and and_109 (and_109_out, JMS, AUTOIND, PH06);
  and and_110 (and_110_out, JMS, AUTOIND, PH07);
  and and_111 (and_111_out, JMS, AUTOIND, PH08);
  and and_112 (and_112_out, JMS, AUTOIND, PH09);
  and and_113 (and_113_out, JMS, AUTOIND, PH10);
  and and_114 (and_114_out, JMS, AUTOIND, PH11);
  LED led_185 (.in(CNT_JMS_IA));
  LED led_186 (.in(and_106_out));
  LED led_187 (.in(and_107_out));
  LED led_188 (.in(and_108_out));
  LED led_189 (.in(and_109_out));
  LED led_190 (.in(and_110_out));
  LED led_191 (.in(and_111_out));
  LED led_192 (.in(and_112_out));
  LED led_193 (.in(and_113_out));
  LED led_194 (.in(and_114_out));
  assign IR2RAMA = CNT_JMS_IA ? CNT_JMS_IA : 1'bz;  // Driver driver_394
  assign RAM_OE = CNT_JMS_IA ? CNT_JMS_IA : 1'bz;  // Driver driver_395
  assign driver_396_out = CNT_JMS_IA ? CNT_JMS_IA : 1'bz;  // Driver driver_396
  assign driver_397_out = CNT_JMS_IA ? CNT_JMS_IA : 1'bz;  // Driver driver_397
  assign driver_398_out = CNT_JMS_IA ? CNT_JMS_IA : 1'bz;  // Driver driver_398
  assign IR2RAMA = and_106_out ? and_106_out : 1'bz;  // Driver driver_399
  assign IND_CK = and_106_out ? and_106_out : 1'bz;  // Driver driver_400
  assign RAM_OE = and_106_out ? and_106_out : 1'bz;  // Driver driver_401
  assign driver_402_out = and_106_out ? and_106_out : 1'bz;  // Driver driver_402
  assign driver_403_out = and_106_out ? and_106_out : 1'bz;  // Driver driver_403
  assign INC2RAMD = and_107_out ? and_107_out : 1'bz;  // Driver driver_404
  assign RAM_WE = and_107_out ? and_107_out : 1'bz;  // Driver driver_405
  assign IND2INC = and_107_out ? and_107_out : 1'bz;  // Driver driver_406
  Driver driver_407 (.in(and_107_out), .en(and_107_out));  // open: out
  assign driver_408_out = and_107_out ? and_107_out : 1'bz;  // Driver driver_408
  assign IR2RAMA = and_108_out ? and_108_out : 1'bz;  // Driver driver_409
  assign RAMD2IND = and_108_out ? and_108_out : 1'bz;  // Driver driver_410
  assign RAM_OE = and_108_out ? and_108_out : 1'bz;  // Driver driver_411
  assign driver_412_out = and_108_out ? and_108_out : 1'bz;  // Driver driver_412
  assign driver_413_out = and_108_out ? and_108_out : 1'bz;  // Driver driver_413
  assign IR2RAMA = and_109_out ? and_109_out : 1'bz;  // Driver driver_414
  assign RAMD2IND = and_109_out ? and_109_out : 1'bz;  // Driver driver_415
  assign RAM_OE = and_109_out ? and_109_out : 1'bz;  // Driver driver_416
  assign IND_CK = and_109_out ? and_109_out : 1'bz;  // Driver driver_417
  assign driver_418_out = and_109_out ? and_109_out : 1'bz;  // Driver driver_418
  assign IND2RAMA = and_110_out ? and_110_out : 1'bz;  // Driver driver_419
  assign PC2RAMD = and_110_out ? and_110_out : 1'bz;  // Driver driver_420
  Driver driver_421 (.in(and_110_out), .en(and_110_out));  // open: out
  assign driver_422_out = and_110_out ? and_110_out : 1'bz;  // Driver driver_422
  assign driver_423_out = and_110_out ? and_110_out : 1'bz;  // Driver driver_423
  assign IND2RAMA = and_111_out ? and_111_out : 1'bz;  // Driver driver_424
  assign PC2RAMD = and_111_out ? and_111_out : 1'bz;  // Driver driver_425
  assign RAM_WE = and_111_out ? and_111_out : 1'bz;  // Driver driver_426
  assign PC_LD = and_111_out ? and_111_out : 1'bz;  // Driver driver_427
  assign IND2PC = and_111_out ? and_111_out : 1'bz;  // Driver driver_428
  assign IND2PC = and_112_out ? and_112_out : 1'bz;  // Driver driver_429
  assign PC_LD = and_112_out ? and_112_out : 1'bz;  // Driver driver_430
  assign PC_CK = and_112_out ? and_112_out : 1'bz;  // Driver driver_431
  Driver driver_432 (.in(and_112_out), .en(and_112_out));  // open: out
  assign driver_433_out = and_112_out ? and_112_out : 1'bz;  // Driver driver_433
  Driver driver_434 (.in(and_113_out), .en(and_113_out));  // open: out
  Driver driver_435 (.in(and_113_out), .en(and_113_out));  // open: out
  assign driver_436_out = and_113_out ? and_113_out : 1'bz;  // Driver driver_436
  assign driver_437_out = and_113_out ? and_113_out : 1'bz;  // Driver driver_437
  assign driver_438_out = and_113_out ? and_113_out : 1'bz;  // Driver driver_438
  assign PC_CK = and_114_out ? and_114_out : 1'bz;  // Driver driver_439
  assign driver_440_out = and_114_out ? and_114_out : 1'bz;  // Driver driver_440
  assign driver_441_out = and_114_out ? and_114_out : 1'bz;  // Driver driver_441
  assign driver_442_out = and_114_out ? and_114_out : 1'bz;  // Driver driver_442
  Driver driver_443 (.in(and_114_out), .en(and_114_out));  // open: out
  and and_115 (CNT_JMP, JMP, NOIND, PH02);
  and and_116 (and_116_out, JMP, NOIND, PH03);
  LED led_195 (.in(CNT_JMP));
  LED led_196 (.in(and_116_out));
  assign IR2PC = CNT_JMP ? CNT_JMP : 1'bz;  // Driver driver_444
  assign driver_445_out = CNT_JMP ? CNT_JMP : 1'bz;  // Driver driver_445
  assign driver_446_out = CNT_JMP ? CNT_JMP : 1'bz;  // Driver driver_446
  assign driver_447_out = CNT_JMP ? CNT_JMP : 1'bz;  // Driver driver_447
  assign driver_448_out = CNT_JMP ? CNT_JMP : 1'bz;  // Driver driver_448
  assign IR2PC = and_116_out ? and_116_out : 1'bz;  // Driver driver_449
  assign PC_LD = and_116_out ? and_116_out : 1'bz;  // Driver driver_450
  assign PC_CK = and_116_out ? and_116_out : 1'bz;  // Driver driver_451
  assign driver_452_out = and_116_out ? and_116_out : 1'bz;  // Driver driver_452
  assign driver_453_out = and_116_out ? and_116_out : 1'bz;  // Driver driver_453
  and and_117 (CNT_JMP_I, JMP, IND, PH02);
  and and_118 (and_118_out, JMP, IND, PH03);
  LED led_197 (.in(CNT_JMP_I));
  LED led_198 (.in(and_118_out));
  assign IR2RAMA = CNT_JMP_I ? CNT_JMP_I : 1'bz;  // Driver driver_454
  assign RAMD2PC = CNT_JMP_I ? CNT_JMP_I : 1'bz;  // Driver driver_455
  assign RAM_OE = CNT_JMP_I ? CNT_JMP_I : 1'bz;  // Driver driver_456
  assign driver_457_out = CNT_JMP_I ? CNT_JMP_I : 1'bz;  // Driver driver_457
  assign driver_458_out = CNT_JMP_I ? CNT_JMP_I : 1'bz;  // Driver driver_458
  assign IR2RAMA = and_118_out ? and_118_out : 1'bz;  // Driver driver_459
  assign RAMD2PC = and_118_out ? and_118_out : 1'bz;  // Driver driver_460
  assign RAM_OE = and_118_out ? and_118_out : 1'bz;  // Driver driver_461
  assign PC_LD = and_118_out ? and_118_out : 1'bz;  // Driver driver_462
  assign PC_CK = and_118_out ? and_118_out : 1'bz;  // Driver driver_463
  and and_119 (CNT_JMP_IA, JMP, AUTOIND, PH02);
  and and_120 (and_120_out, JMP, AUTOIND, PH03);
  and and_121 (and_121_out, JMP, AUTOIND, PH04);
  and and_122 (and_122_out, JMP, AUTOIND, PH05);
  and and_123 (and_123_out, JMP, AUTOIND, PH06);
  LED led_199 (.in(CNT_JMP_IA));
  LED led_200 (.in(and_120_out));
  LED led_201 (.in(and_121_out));
  LED led_202 (.in(and_122_out));
  LED led_203 (.in(and_123_out));
  assign IR2RAMA = CNT_JMP_IA ? CNT_JMP_IA : 1'bz;  // Driver driver_464
  assign RAM_OE = CNT_JMP_IA ? CNT_JMP_IA : 1'bz;  // Driver driver_465
  assign driver_466_out = CNT_JMP_IA ? CNT_JMP_IA : 1'bz;  // Driver driver_466
  assign driver_467_out = CNT_JMP_IA ? CNT_JMP_IA : 1'bz;  // Driver driver_467
  assign driver_468_out = CNT_JMP_IA ? CNT_JMP_IA : 1'bz;  // Driver driver_468
  assign IR2RAMA = and_120_out ? and_120_out : 1'bz;  // Driver driver_469
  assign IND_CK = and_120_out ? and_120_out : 1'bz;  // Driver driver_470
  assign RAM_OE = and_120_out ? and_120_out : 1'bz;  // Driver driver_471
  assign driver_472_out = and_120_out ? and_120_out : 1'bz;  // Driver driver_472
  assign driver_473_out = and_120_out ? and_120_out : 1'bz;  // Driver driver_473
  assign INC2RAMD = and_121_out ? and_121_out : 1'bz;  // Driver driver_474
  assign RAM_WE = and_121_out ? and_121_out : 1'bz;  // Driver driver_475
  assign IND2INC = and_121_out ? and_121_out : 1'bz;  // Driver driver_476
  assign driver_477_out = and_121_out ? and_121_out : 1'bz;  // Driver driver_477
  assign driver_478_out = and_121_out ? and_121_out : 1'bz;  // Driver driver_478
  assign IR2RAMA = and_122_out ? and_122_out : 1'bz;  // Driver driver_479
  assign RAMD2PC = and_122_out ? and_122_out : 1'bz;  // Driver driver_480
  assign RAM_OE = and_122_out ? and_122_out : 1'bz;  // Driver driver_481
  assign driver_482_out = and_122_out ? and_122_out : 1'bz;  // Driver driver_482
  assign driver_483_out = and_122_out ? and_122_out : 1'bz;  // Driver driver_483
  assign IR2RAMA = and_123_out ? and_123_out : 1'bz;  // Driver driver_484
  assign RAMD2PC = and_123_out ? and_123_out : 1'bz;  // Driver driver_485
  assign RAM_OE = and_123_out ? and_123_out : 1'bz;  // Driver driver_486
  assign PC_LD = and_123_out ? and_123_out : 1'bz;  // Driver driver_487
  assign PC_CK = and_123_out ? and_123_out : 1'bz;  // Driver driver_488
  and and_124 (CNT_OPR1, OPR1, NOTNOP, PH02);
  and and_125 (and_125_out, OPR1, 1'b1, PH03);
  LED led_204 (.in(CNT_OPR1));
  LED led_205 (.in(and_125_out));
  assign ROT2AC = CNT_OPR1 ? CNT_OPR1 : 1'bz;  // Driver driver_489
  Driver driver_490 (.in(CNT_OPR1), .en(CNT_OPR1));  // open: out
  Driver driver_491 (.in(CNT_OPR1), .en(CNT_OPR1));  // open: out
  Driver driver_492 (.in(CNT_OPR1), .en(CNT_OPR1));  // open: out
  Driver driver_493 (.in(CNT_OPR1), .en(CNT_OPR1));  // open: out
  assign AC_CK = and_125_out ? and_125_out : 1'bz;  // Driver driver_494
  assign LINK_CK = and_125_out ? and_125_out : 1'bz;  // Driver driver_495
  assign ROT2AC = and_125_out ? and_125_out : 1'bz;  // Driver driver_496
  Driver driver_497 (.in(and_125_out), .en(and_125_out));  // open: out
  Driver driver_498 (.in(and_125_out), .en(and_125_out));  // open: out
  Driver driver_499 (.in(and_125_out), .en(and_125_out));  // open: out
  and and_126 (CNT_OPR2, OPR2, NOTNOP, PH02);
  and and_127 (and_127_out, OPR2, 1'b1, PH03);
  and and_128 (and_128_out, OPR2, SKIP, PH04);
  assign ROT2AC = CNT_OPR2 ? CNT_OPR2 : 1'bz;  // Driver driver_500
  LED led_206 (.in(CNT_OPR2));
  Driver driver_501 (.in(CNT_OPR2), .en(CNT_OPR2));  // open: out
  Driver driver_502 (.in(CNT_OPR2), .en(CNT_OPR2));  // open: out
  Driver driver_503 (.in(CNT_OPR2), .en(CNT_OPR2));  // open: out
  Driver driver_504 (.in(CNT_OPR2), .en(CNT_OPR2));  // open: out
  assign AC_CK = and_127_out ? and_127_out : 1'bz;  // Driver driver_505
  LED led_207 (.in(and_127_out));
  assign ROT2AC = and_127_out ? and_127_out : 1'bz;  // Driver driver_506
  assign LINK_CK = and_127_out ? and_127_out : 1'bz;  // Driver driver_507
  Driver driver_508 (.in(and_127_out), .en(and_127_out));  // open: out
  Driver driver_509 (.in(and_127_out), .en(and_127_out));  // open: out
  assign IR_CK = and_128_out ? and_128_out : 1'bz;  // Driver driver_510
  LED led_208 (.in(and_128_out));
  assign PC_CK = and_128_out ? and_128_out : 1'bz;  // Driver driver_511
  Driver driver_512 (.in(and_128_out), .en(and_128_out));  // open: out
  Driver driver_513 (.in(and_128_out), .en(and_128_out));  // open: out
  Driver driver_514 (.in(and_128_out), .en(and_128_out));  // open: out

  // Other names for the same wires on the sheet: RAMADDR[11:0] = {RA3, RA2, RA1, RA0}; PI0[2:0] = PCIN[2:0];
  //   PI1[2:0] = PCIN[5:3]; PI2[2:0] = PCIN[8:6]; PI3[2:0] = PCIN[11:9]; AC0[2:0] = AC[2:0]; AC1[2:0] = AC[5:3];
  //   AC2[2:0] = AC[8:6]; AC3[2:0] = AC[11:9]; IR0[2:0] = BUS_IR[2:0]; IR1[2:0] = BUS_IR[5:3]; IR2[2:0] = BUS_IR[8:6];
  //   MP = BUS_IR[7]; IR3[2:0] = BUS_IR[11:9]; PC0[2:0] = BUS_PC[2:0]; PC1[2:0] = BUS_PC[5:3]; PC2[2:0] = BUS_PC[8:6];
  //   PC3[2:0] = BUS_PC[11:9]; DATA[11:0] = {DA3, DA2, DA1, DA0}; INDOUT[11:0] = {IND3, IND2, IND1, IND0};
  //   RD0[2:0] = RAMDATA[2:0]; RD1[2:0] = RAMDATA[5:3]; RD2[2:0] = RAMDATA[8:6]; RD3[2:0] = RAMDATA[11:9]

  // Notes on the sheet:
  //   clk: Hz: 10000
  //   IOT DECODER
  //   PH0 & PH1
  //   IR DECODER
  //   OPR DECODER
  //   PC
  //   IR
  //   AC
  //   IND
  //   RAM-A
  //   RAM-D
  //   PC-IN
  //   DATA
  //   KCF
  //   CLA
  //   AND
  //   KSF
  //   CLL
  //   TAD
  //   KCC
  //   KRS
  //   CMA
  //   CML
  //   ISZ
  //   DCA
  //   KIE
  //   IAC
  //   JMS
  //   STATE
  //   INSTRUCTION
  //   RUN
  //   HALT
  //   PC=0200
  //   BREAKPOINT
  //   PCIN
  //   KRB
  //   ROR
  //   JMP
  //   TFL
  //   ROL
  //   x2
  //   IOT
  //   OPR
  //   TSF
  //   START/STOP/STEP
  //   CLOCK CYCLE CONTROLLER
  //   TCF
  //   SMA
  //   DIR
  //   PCOUT
  //   TPC
  //   TSK
  //   SZA
  //   SNL
  //   AUTO
  //   IND
  //   TLS
  //   INV
  //   CURR
  //   PAGE
  //   OSR
  //   RAMADDR
  //   HLT
  //   -
  //   NOP
  //   contents of eeprom_1 (hex, n*v repeats v):
  //   0,a01,2,3,0,0,f02,e00,0,f02,f02,f02,f02,f02,f02,f02,0,1,2,3,4,6,8,c,10,18,20,30,40,
  //   60,80,c0,100,180,200,29c,300,400,600,6ca,800,fcf,ffe,ffd,ffb,ff7,fef,fdf,e7f,fbf,
  //   f7f,eff,dff,bff,7ff,fff,aaa,555,c00,e00,f00,f80,fe0,ff0,ff8,ffc,7,37,f,1f,3f,7f,ff,
  //   1ff,3ff,fc0,a95,56a,1f8,e07,87,a60,a60,f02,f02,f02,f02,f02,f02,f02,f02,f02,f02,f02,
  //   f02,f02,f02,f02,f02,f02,237,e80,f02,f08,f02,e80,f20,f02,f28,f08,f02,e80,228,f20,f08,
  //   f02,f28,f02,e80,225,f20,f08,f02,f28,f02,e00,e00,f08,a64,e80,222,f20,f08,f02,f28,f02,
  //   e80,220,f20,f08,f02,f28,f02,e80,21e,f20,f08,f02,f28,f02,e80,21c,f20,f08,f02,f28,f02,
  //   e80,21a,f20,f08,f02,f28,f02,e80,218,f20,f08,f02,f28,f02,e80,216,f20,f08,f02,f28,f02,
  //   e80,214,f20,f08,f02,f28,f02,e80,212,f20,f08,f02,f28,f02,e80,211,f20,f08,f02,f28,f02,
  //   e80,236,f48,f02,e80,228,f48,f08,f02,e80,236,f40,f08,f02,e80,228,f40,f02,e80,237,e20,
  //   f20,f02,e80,239,e20,f28,f02,239,e20,f20,f02,e80,238,e20,f28,f02,238,e20,f20,f02,e80,
  //   237,e20,f20,f02,e80,e01,f20,f08,f02,e80,237,e01,f20,f02,e80,241,e01,e01,e01,e01,f20,
  //   f02,e80,e40,e04,f18,f02,e80,e40,e10,228,e04,f18,f08,f02,e80,e40,e04,f10,f08,f02,e80,
  //   e40,e10,228,e04,f10,f02,e80,228,e04,f10,aaa,e40,f18,f02,aae,e10,f10,f02,aa6,e40,f18,
  //   f02,e10,f10,f02,e10,f18,f02,e80,237,f80,f20,f02,e80,f04,e20,f20,f02,e80,e40,e00,f28,
  //   f18,f02,e80,e40,f00,f28,f18,f02,e80,236,228,e20,f20,f02,e80,235,225,e20,f20,f02,e80,
  //   234,222,e20,f20,f02,e80,233,220,e20,f20,f02,e80,232,21e,e20,f20,f02,e80,231,21c,e20,
  //   f20,f02,e80,22f,21a,e20,f20,f02,e80,22e,218,e20,f20,f02,e80,22d,216,e20,f20,f02,e80,
  //   22c,214,e20,f20,f02,e80,22b,212,e20,f20,f02,e80,22a,211,e20,f20,f02,e80,e40,228,228,
  //   f18,f20,f02,e80,e40,23a,225,f18,f20,f02,e80,e40,23b,222,f18,f20,f02,e80,e40,23c,220,
  //   f18,f20,f02,e80,e40,23d,21e,f18,f20,f02,e80,e40,24b,21c,f18,f20,f02,e80,e40,23e,21a,
  //   f18,f20,f02,e80,e40,23f,218,f18,f20,f02,e80,e40,240,216,f18,f20,f02,e80,e40,241,214,
  //   f18,f20,f02,e80,e40,22a,212,f18,f20,f02,e80,e40,237,211,f18,f20,f02,e80,e40,e10,228,
  //   228,f10,f20,f02,e80,e40,236,225,225,e20,f10,f20,f02,e80,e40,235,222,222,e20,f10,f20,
  //   f02,e80,e40,234,220,220,e20,f10,f20,f02,e80,e40,233,21e,21e,e20,f10,f20,f02,e80,e40,
  //   232,21c,21c,e20,f10,f20,f02,e80,e40,231,21a,21a,e20,f10,f20,f02,e80,e40,22f,218,218,
  //   e20,f10,f20,f02,e80,e40,22e,216,216,e20,f10,f20,f02,e80,e40,22d,214,214,e20,f10,f20,
  //   f02,e80,e40,22c,212,212,e20,f10,f20,f02,e80,e40,22b,211,211,e20,f10,f18,f02,e80,e40,
  //   211,213,22c,e20,f10,f20,f02,e80,e40,212,215,22d,e20,f10,f20,f02,e80,e40,214,217,22e,
  //   e20,f10,f20,f02,e80,e40,216,219,22f,e20,f10,f20,f02,e80,e40,218,21b,231,e20,f10,f20,
  //   f02,e80,e40,21a,21d,232,e20,f10,f20,f02,e80,e40,21c,21f,233,e20,f10,f20,f02,e80,e40,
  //   21e,221,234,e20,f10,f20,f02,e80,e40,220,224,235,e20,f10,f20,f02,e80,e40,222,226,236,
  //   e20,f10,f20,f02,e80,e40,225,23a,f18,f20,f02,e80,e40,237,211,f18,f20,f02,e80,e40,213,
  //   213,240,211,e20,f10,f20,f02,e80,e40,215,215,23f,213,e20,f10,f20,f02,e80,e40,217,217,
  //   23e,242,e20,f10,f20,f02,e80,e40,219,219,229,e20,f10,f20,f02,e80,e40,21b,21b,23d,245,
  //   e20,f10,f20,f02,e80,e40,21d,21d,23c,246,e20,f10,f20,f02,e80,e40,21f,21f,230,e20,f10,
  //   f20,f02,e80,e40,221,221,23a,248,e20,f10,f20,f02,e80,e40,224,224,228,249,e20,f10,f20,
  //   f02,e80,e40,226,226,24a,e20,f10,f20,f02,e80,e40,23a,23a,236,e20,f18,f20,f02,e80,e40,
  //   237,237,211,e20,f18,f20,f02,e80,e40,211,e08,f10,f02,e80,e40,210,e08,f20,f02,e80,e40,
  //   210,e08,f18,f02,e80,e40,e10,210,e08,f18,f02,e80,e40,e10,237,e08,e20,f20,f02,e80,e40,
  //   e10,210,e08,236,e20,f28,f18,f02,e80,e40,228,e08,235,e20,f28,f18,f02,e80,e40,225,e08,
  //   234,e20,f28,f18,f02,e80,e40,222,e08,233,e20,f28,f18,f02,e80,e40,220,e08,232,e20,f28,
  //   f18,f02,e80,e40,21e,e08,231,e20,f28,f18,f02,e80,e40,21c,e08,22f,e20,f28,f18,f02,e80,
  //   e40,21a,e08,22e,e20,f28,f18,f02,e80,e40,218,e08,22d,e20,f28,f18,f02,e80,e40,216,e08,
  //   22c,e20,f28,f18,f02,e80,e40,214,e08,22b,e20,f28,f18,f02,e80,e40,212,e08,22a,e20,f28,
  //   f18,f02,e80,e40,211,e08,237,e20,f28,f10,f02,e80,e40,212,e0a,f10,f02,e80,e40,210,e0a,
  //   f20,f02,e80,e40,210,e0a,f18,f02,e80,e40,e10,210,e0a,f18,f02,e80,e40,e10,237,e0a,e20,
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  //   RAMDATA
  //   INDOUT
  //   AUTOINDEX
  //   INDIRECT
  //   AND
  //   STEP1
  //   LATCHED
  //   DATA
  //   IND
  //   STEP1
  //   IND
  //   STEP2
  //   AND
  //   STEP2
  //   AND i
  //   AND-i-auto
  //   iAuto 1
  //   iAuto 2
  //   iAuto 3
  //   TAD
  //   STEP1
  //   TAD
  //   STEP2
  //   TAD i
  //   TAD-i-auto
  //   Get address
  //   of M
  //   Save value
  //   from M
  //   indo LATDAT
  //   SKIP IF
  //   AC=ZERO
  //   ISZ i
  //   Save value
  //   from IND
  //   indo LATDAT
  //   ISZ-i-auto
  //   DCA i
  //   DCA-i-auto
  //   Prepare to store
  //   return address
  //   Actually store
  //   return address
  //   Actually increment
  //   PC
  //   Actually set
  //   PC
  //   Pause to accept
  //   new PC inc clk
  //   Prepate to store 
  //   return addr
  //   to [ind]
  //   Store return addr
  //   to [ind]
  //   JMS i
  //   JMS i-auto
  //   Prepare to set
  //   new PC
  //   Actually set
  //   new PC
  //   Prepare to set PC
  //   with new vector
  //   JMP i
  //   JMP i-auto
  //   OPR 1
  //   OPR 2
endmodule
